// Logisim project SPI interface.circ as structural Verilog
module SPI_module__cell (
  input  CS,
  input  CLK,
  input  MOSI,
  input  err,
  input  [10:0] energy_in,
  input  [3:0] type_select_in,
  input  [1:0] player_select_in,
  output clk_out,
  output is_selected,
  output move_end_1,
  output move_end_2,
  output [1:0] is_task,
  output task_conf,
  output [4:0] command,
  output transanction_end,
  output [10:0] energy_out,
  output [1:0] type_select_out,
  output [1:0] player_select_out,
  output MISO
);

  wire and_2_out, not_1_out, or_1_out, or_2_out, special_sequence_decoder_1_is_transancition;
  wire [3:0] command_buffer_1_buffer_ptr;
  wire [15:0] command_buffer_1_data_out;

  and and_1 (clk_out, CS, CLK);
  not not_1 (not_1_out, CS);
  and and_2 (and_2_out, special_sequence_decoder_1_is_transancition, clk_out);
  or or_1 (or_1_out, not_1_out, special_sequence_decoder_1_is_transancition);
  transactio_parser transactio_parser_1 (
    .CLK(and_2_out), .MOSI(MOSI), .Reset(not_1_out), .Command(command), .Energy(energy_out),
    .Data_ready(transanction_end));
  command_buffer command_buffer_1 (
    .MOSI(MOSI), .CLK(clk_out), .Reset(or_1_out), .Data_out(command_buffer_1_data_out),
    .buffer_ptr(command_buffer_1_buffer_ptr));
  special_sequence_decoder special_sequence_decoder_1 (
    .Data(command_buffer_1_data_out), .Buffer_pointer(command_buffer_1_buffer_ptr), .RST(not_1_out),
    .move_end_1(move_end_1), .is_transancition(special_sequence_decoder_1_is_transancition),
    .move_end_2(move_end_2), .is_task(is_task), .is_selected(is_selected));  // open: ERR
  or or_2 (or_2_out, is_task[0], is_task[1]);
  and and_3 (task_conf, or_2_out, clk_out, MOSI);

  // Other names for the same wires on the sheet: clk_t = clk_out

  // Notes on the sheet:
  //   type_select_out: pull=down
  //   is_task: pull=down
  //   player_select_in: pull=down
  //   type_select_in: pull=down
  //   energy_out: pull=down
  //   energy_in: pull=down
  //   CLK: pull=down
  //   err: pull=down
  //   command: pull=down
  //   player_select_out: pull=down
  //   MOSI: pull=down
endmodule

module command_buffer (
  input  MOSI,
  input  CLK,
  input  Reset,
  output [15:0] Data_out,
  output [3:0] buffer_ptr
);

  Register #(.width(16)) register_1 (.D({Data_out[14:0], MOSI}), .Q(Data_out), .clk(CLK), .clr(Reset));  // open: en
  Counter #(.width(4), .max('hf)) counter_1 (.Q(buffer_ptr), .clk(CLK), .clr(Reset));  // open: load, D, count, carry

  // Notes on the sheet:
  //   buffer_ptr: pull=down
  //   CLK: pull=down
  //   Reset: pull=down
  //   MOSI: pull=down
  //   Data_out: pull=down
endmodule

module special_sequence_decoder (
  input  [15:0] Data,
  input  [3:0] Buffer_pointer,
  input  RST,
  output move_end_1,
  output is_transancition,
  output is_selected,
  output move_end_2,
  output [1:0] is_task,
  output ERR
);

  wire and_1_out, and_2_out, and_3_out, and_4_out, and_5_out, and_6_out, comparator_1_eq, comparator_2_eq,
       comparator_3_eq, comparator_4_eq, comparator_5_eq, comparator_6_eq, comparator_7_eq, comparator_8_eq,
       comparator_8_gt, lock, or_1_out, xor_1_out;

  Comparator #(.width(16)) comparator_1 (.a(Data), .b(16'h8000), .eq(comparator_1_eq));  // open: gt, lt
  Comparator #(.width(16)) comparator_2 (.a(Data), .b(16'h4000), .eq(comparator_2_eq));  // open: gt, lt
  Comparator #(.width(16)) comparator_3 (.a(Data), .b(16'h2000), .eq(comparator_3_eq));  // open: gt, lt
  Comparator #(.width(16)) comparator_4 (.a(Data), .b(16'hc000), .eq(comparator_4_eq));  // open: gt, lt
  Comparator #(.width(4)) comparator_5 (.a(Buffer_pointer), .b(4'b0001), .eq(comparator_5_eq));  // open: gt, lt
  Comparator #(.width(4)) comparator_6 (.a(Buffer_pointer), .b(4'b0010), .eq(comparator_6_eq));  // open: gt, lt
  Comparator #(.width(4)) comparator_7 (.a(Buffer_pointer), .b(4'b0011), .eq(comparator_7_eq));  // open: gt, lt
  Comparator #(.width(4)) comparator_8 (
    .a(Buffer_pointer), .b(4'b0101), .gt(comparator_8_gt), .eq(comparator_8_eq));  // open: lt
  and and_1 (and_1_out, comparator_1_eq, comparator_5_eq);
  and and_2 (and_2_out, comparator_2_eq, comparator_6_eq);
  and and_3 (and_3_out, comparator_3_eq, comparator_7_eq);
  and and_4 (and_4_out, comparator_4_eq, comparator_6_eq);
  xor xor_1 (xor_1_out, Data[11], Data[12]);
  and and_5 (and_5_out, Data[12], comparator_8_eq, Data[11]);
  and and_6 (and_6_out, xor_1_out, comparator_8_eq);
  or or_1 (or_1_out, and_5_out, and_6_out, and_4_out, and_3_out, and_2_out);
  D_Flip_Flop d_ff_1 (.clk(lock), .D(and_2_out), .Q(is_transancition), .reset(RST));  // open: Qn, preset, en
  D_Flip_Flop d_ff_2 (.clk(lock), .D(and_3_out), .Q(is_selected), .reset(RST));  // open: Qn, preset, en
  D_Flip_Flop d_ff_3 (.clk(lock), .D(and_4_out), .Q(move_end_2), .reset(RST));  // open: Qn, preset, en
  D_Flip_Flop d_ff_4 (.clk(lock), .D(and_6_out), .Q(is_task[0]), .reset(RST));  // open: Qn, preset, en
  D_Flip_Flop d_ff_5 (.clk(lock), .D(and_5_out), .Q(is_task[1]), .reset(RST));  // open: Qn, preset, en
  D_Flip_Flop d_ff_6 (.clk(or_1_out), .D(1'b1), .Q(lock), .reset(RST));  // open: Qn, preset, en
  and and_7 (move_end_1, ~lock, and_1_out);  // AND_Gate
  and and_8 (ERR, lock, comparator_8_gt);

  // Notes on the sheet:
  //   ERR: pull=down
  //   Buffer_pointer: pull=down
  //   Data: pull=down
  //   RST: pull=down
endmodule

module transactio_parser (
  input  CLK,
  input  MOSI,
  input  Reset,
  output [4:0] Command,
  output [10:0] Energy,
  output Data_ready
);

  wire and_1_out, and_2_out, and_3_out, d_ff_1_q, nor_1_out, nor_2_out;
  wire [3:0] command_buffer_1_buffer_ptr, xor_1_out;
  wire [15:11] command_buffer_1_data_out;

  and and_1 (and_1_out, ~Data_ready, CLK);  // AND_Gate
  command_buffer command_buffer_1 (
    .MOSI(MOSI), .CLK(and_1_out), .Reset(Reset), .Data_out({command_buffer_1_data_out, Energy}),
    .buffer_ptr(command_buffer_1_buffer_ptr));
  assign xor_1_out = command_buffer_1_buffer_ptr ^ 4'b0101;  // XOR_Gate xor_1, 4 bits wide
  nor nor_1 (nor_1_out, command_buffer_1_buffer_ptr[0], command_buffer_1_buffer_ptr[1], command_buffer_1_buffer_ptr[3], command_buffer_1_buffer_ptr[2]);
  Register #(.width(5)) register_1 (.D(Energy[4:0]), .en(1'b1), .Q(Command), .clk(d_ff_1_q), .clr(Reset));
  nor nor_2 (nor_2_out, xor_1_out[0], xor_1_out[1], xor_1_out[3], xor_1_out[2]);
  D_Flip_Flop #(.trigger("high")) d_ff_1 (
    .clk(nor_2_out), .D(nor_2_out), .Q(d_ff_1_q), .reset(Reset));  // open: Qn, preset, en
  and and_2 (and_2_out, Command[3], d_ff_1_q);
  or or_1 (Data_ready, and_2_out, and_3_out);
  and and_3 (and_3_out, d_ff_1_q, nor_1_out);
endmodule

module command_decoder (
  input  [4:0] in_1
);
endmodule
