// Logisim project display controller.circ as structural Verilog: 18 circuits, main circuit Locccal test
module Locccal_test (
  input  [9:0] in_1
);

  wire [4:0] inversion_1_out_2, inversion_1_out_3, inversion_1_out_4, inversion_1_out_5, inversion_1_out_6,
       inversion_1_out_7, inversion_1_out_8, inversion_1_out_9, inversion_1_out_10, inversion_1_out_11,
       inversion_1_out_12, output_numder_1_out_2, output_numder_1_out_3, output_numder_1_out_4,
       output_numder_1_out_5, output_numder_1_out_6, output_numder_1_out_7, output_numder_1_out_8,
       output_numder_1_out_9, output_numder_1_out_10, output_numder_1_out_11, output_numder_1_out_12;

  DotMatrix #(.matrixcols(11), .matrixrows(5)) dotmatrix_1 (
    .col0(output_numder_1_out_2), .col1(output_numder_1_out_3), .col2(output_numder_1_out_4),
    .col3(output_numder_1_out_5), .col4(output_numder_1_out_6), .col5(output_numder_1_out_7),
    .col6(output_numder_1_out_8), .col7(output_numder_1_out_9), .col8(output_numder_1_out_10),
    .col9(output_numder_1_out_11), .col10(output_numder_1_out_12));
  Output_Numder output_numder_1 (
    .Energy(in_1), .out_2(output_numder_1_out_2), .out_3(output_numder_1_out_3),
    .out_4(output_numder_1_out_4), .out_5(output_numder_1_out_5), .out_6(output_numder_1_out_6),
    .out_7(output_numder_1_out_7), .out_8(output_numder_1_out_8), .out_9(output_numder_1_out_9),
    .out_10(output_numder_1_out_10), .out_11(output_numder_1_out_11), .out_12(output_numder_1_out_12));
  inversion inversion_1 (
    .in_1(in_1), .out_2(inversion_1_out_2), .out_3(inversion_1_out_3), .out_4(inversion_1_out_4),
    .out_5(inversion_1_out_5), .out_6(inversion_1_out_6), .out_7(inversion_1_out_7),
    .out_8(inversion_1_out_8), .out_9(inversion_1_out_9), .out_10(inversion_1_out_10),
    .out_11(inversion_1_out_11), .out_12(inversion_1_out_12));
  DotMatrix #(.matrixcols(11), .matrixrows(5)) dotmatrix_2 (
    .col0(inversion_1_out_2), .col1(inversion_1_out_3), .col2(inversion_1_out_4), .col3(inversion_1_out_5),
    .col4(inversion_1_out_6), .col5(inversion_1_out_7), .col6(inversion_1_out_8), .col7(inversion_1_out_9),
    .col8(inversion_1_out_10), .col9(inversion_1_out_11), .col10(inversion_1_out_12));
endmodule

module Player_move (
  input  [1:0] in_1,
  output [7:0] out_2,
  output [7:0] out_3,
  output [7:0] out_4,
  output [7:0] out_5,
  output [7:0] out_6,
  output [7:0] out_7,
  output [7:0] out_8,
  output [7:0] out_9,
  output [7:0] out_10,
  output [7:0] out_11,
  output [7:0] out_12,
  output [7:0] out_13,
  output [7:0] out_14,
  output [7:0] out_15,
  output [7:0] out_16,
  output [7:0] out_17,
  output [7:0] out_18,
  output [7:0] out_19,
  output [7:0] out_20,
  output [7:0] out_21,
  output [7:0] out_22,
  output [7:0] out_23
);

  Output_Numder output_numder_1 ();  // open: Energy, out_2, out_3, out_4, out_5, out_6, out_7, out_8, out_9, out_10, out_11, out_12
  Transistor #(.width(8)) transistor_1 (.in({8{1'b0}}), .out(out_21), .gate(in_1[1]));
  Transistor #(.width(8)) transistor_2 (.in({8{1'b0}}), .out(out_23), .gate(in_1[1]));
  Transistor #(.width(8)) transistor_3 (.in({8{1'b0}}), .out(out_22), .gate(in_1[1]));
  Transistor #(.\type ("n"), .width(8)) transistor_4 (.in({8{1'b1}}), .out(out_13), .gate(in_1[1]));
  Transistor #(.\type ("n"), .width(8)) transistor_5 (.in({8{1'b1}}), .out(out_15), .gate(in_1[1]));
  Transistor #(.\type ("n"), .width(8)) transistor_6 (.in({8{1'b1}}), .out(out_14), .gate(in_1[1]));
  Transistor #(.width(8)) transistor_7 (.in({8{1'b0}}), .out(out_11), .gate(in_1[0]));
  Transistor #(.width(8)) transistor_8 (.in({8{1'b0}}), .out(out_12), .gate(in_1[0]));
  Transistor #(.\type ("n"), .width(8)) transistor_9 (.in({8{1'b1}}), .out(out_3), .gate(in_1[0]));
  Transistor #(.\type ("n"), .width(8)) transistor_10 (.in({8{1'b1}}), .out(out_2), .gate(in_1[0]));
  Transistor #(.width(8)) transistor_11 (.in({8{1'b0}}), .out(out_19), .gate(in_1[1]));
  Transistor #(.width(8)) transistor_12 (.in({8{1'b0}}), .out(out_17), .gate(in_1[1]));
  Transistor #(.width(8)) transistor_13 (.in({8{1'b0}}), .out(out_20), .gate(in_1[1]));
  Transistor #(.width(8)) transistor_14 (.in({8{1'b0}}), .out(out_18), .gate(in_1[1]));
  Transistor #(.\type ("n"), .width(8)) transistor_15 (.in({8{1'b1}}), .out(out_17), .gate(in_1[1]));
  Transistor #(.\type ("n"), .width(8)) transistor_16 (.in({8{1'b1}}), .out(out_19), .gate(in_1[1]));
  Transistor #(.\type ("n"), .width(8)) transistor_17 (.in({8{1'b1}}), .out(out_16), .gate(in_1[1]));
  Transistor #(.\type ("n"), .width(8)) transistor_18 (.in({8{1'b1}}), .out(out_18), .gate(in_1[1]));
  Transistor #(.width(8)) transistor_19 (.in({8{1'b0}}), .out(out_9), .gate(in_1[0]));
  Transistor #(.width(8)) transistor_20 (.in({8{1'b0}}), .out(out_7), .gate(in_1[0]));
  Transistor #(.width(8)) transistor_21 (.in({8{1'b0}}), .out(out_10), .gate(in_1[0]));
  Transistor #(.width(8)) transistor_22 (.in({8{1'b0}}), .out(out_8), .gate(in_1[0]));
  Transistor #(.\type ("n"), .width(8)) transistor_23 (.in({8{1'b1}}), .out(out_7), .gate(in_1[0]));
  Transistor #(.\type ("n"), .width(8)) transistor_24 (.in({8{1'b1}}), .out(out_6), .gate(in_1[0]));
  Transistor #(.\type ("n"), .width(8)) transistor_25 (.in({8{1'b1}}), .out(out_5), .gate(in_1[0]));
  Transistor #(.\type ("n"), .width(8)) transistor_26 (.in({8{1'b1}}), .out(out_4), .gate(in_1[0]));
  Transistor #(.width(8)) transistor_27 (.in({8{1'b0}}), .out(out_13), .gate(in_1[1]));
  Transistor #(.width(8)) transistor_28 (.in({8{1'b0}}), .out(out_15), .gate(in_1[1]));
  Transistor #(.width(8)) transistor_29 (.in({8{1'b0}}), .out(out_14), .gate(in_1[1]));
  Transistor #(.width(8)) transistor_30 (.in({8{1'b0}}), .out(out_16), .gate(in_1[1]));
  Transistor #(.\type ("n"), .width(8)) transistor_31 (.in({8{1'b1}}), .out(out_23), .gate(in_1[1]));
  Transistor #(.\type ("n"), .width(8)) transistor_32 (.in({8{1'b1}}), .out(out_22), .gate(in_1[1]));
  Transistor #(.\type ("n"), .width(8)) transistor_33 (.in({8{1'b1}}), .out(out_20), .gate(in_1[1]));
  Transistor #(.\type ("n"), .width(8)) transistor_34 (.in({8{1'b1}}), .out(out_21), .gate(in_1[1]));
  Transistor #(.width(8)) transistor_35 (.in({8{1'b0}}), .out(out_4), .gate(in_1[0]));
  Transistor #(.width(8)) transistor_36 (.in({8{1'b0}}), .out(out_3), .gate(in_1[0]));
  Transistor #(.width(8)) transistor_37 (.in({8{1'b0}}), .out(out_5), .gate(in_1[0]));
  Transistor #(.width(8)) transistor_38 (.in({8{1'b0}}), .out(out_6), .gate(in_1[0]));
  Transistor #(.\type ("n"), .width(8)) transistor_39 (.in({8{1'b1}}), .out(out_10), .gate(in_1[0]));
  Transistor #(.\type ("n"), .width(8)) transistor_40 (.in({8{1'b1}}), .out(out_8), .gate(in_1[0]));
  Transistor #(.\type ("n"), .width(8)) transistor_41 (.in({8{1'b1}}), .out(out_9), .gate(in_1[0]));
  Transistor #(.\type ("n"), .width(8)) transistor_42 (.in({8{1'b1}}), .out(out_11), .gate(in_1[0]));
  Transistor #(.width(8)) transistor_43 (.in({8{1'b0}}), .out(out_2), .gate(in_1[0]));
  Transistor #(.\type ("n"), .width(8)) transistor_44 (.in({8{1'b1}}), .out(out_12), .gate(in_1[0]));
  DotMatrix #(.matrixcols(11), .matrixrows(8)) dotmatrix_1 (
    .col0(out_13), .col1(out_14), .col2(out_15), .col3(out_16), .col4(out_17), .col5(out_18), .col6(out_19),
    .col7(out_20), .col8(out_21), .col9(out_22), .col10(out_23));
  DotMatrix #(.matrixcols(11), .matrixrows(8)) dotmatrix_2 (
    .col0(out_2), .col1(out_3), .col2(out_4), .col3(out_5), .col4(out_6), .col5(out_7), .col6(out_8),
    .col7(out_9), .col8(out_10), .col9(out_11), .col10(out_12));

  // Notes on the sheet:
  //   Оранжевый
  //   Синий
endmodule

module Type (
  input  in_1,
  input  [3:0] in_2,
  output [7:0] out_3,
  output [7:0] out_4,
  output [7:0] out_5,
  output [7:0] out_6,
  output [7:0] out_7,
  output [7:0] out_8,
  output [7:0] out_9,
  output [7:0] out_10,
  output [7:0] out_11,
  output [7:0] out_12,
  output [7:0] out_13
);

  wire and_1_out, and_2_out, decoder_1_out0, decoder_1_out1, decoder_1_out2, decoder_1_out3, decoder_1_out4,
       or_1_out, or_2_out;
  wire [2:2] or_3_out;

  Decoder #(.select(3)) decoder_1 (
    .out0(decoder_1_out0), .out1(decoder_1_out1), .out2(decoder_1_out2), .out3(decoder_1_out3),
    .out4(decoder_1_out4), .sel({or_3_out[2], in_2[1:0]}), .en(or_1_out));  // open: out5, out6, out7
  or or_1 (or_1_out, or_3_out[2], in_1);
  or or_2 (or_2_out, decoder_1_out0, in_2[0], in_2[1], in_2[2], in_2[3]);
  DotMatrix #(.matrixcols(11), .matrixrows(8)) dotmatrix_1 (
    .col0(out_3), .col1(out_4), .col2(out_5), .col3(out_6), .col4(out_7), .col5(out_8), .col6(out_9),
    .col7(out_10), .col8(out_11), .col9(out_12), .col10(out_13));
  Pull_Resistor pull_resistor_1 (.node(decoder_1_out4));
  or or_3 (or_3_out[2], in_2[2], in_2[3]);
  and and_1 (and_1_out, decoder_1_out4, in_2[2]);
  and and_2 (and_2_out, decoder_1_out4, in_2[3]);
  Pull_Resistor pull_resistor_2 (.node(decoder_1_out0));
  Pull_Resistor pull_resistor_3 (.node(decoder_1_out1));
  Pull_Resistor pull_resistor_4 (.node(decoder_1_out3));
  Pull_Resistor pull_resistor_5 (.node(and_2_out));
  Pull_Resistor pull_resistor_6 (.node(and_1_out));
  Pull_Resistor pull_resistor_7 (.node(decoder_1_out2));
  Transistor #(.\type ("n"), .width(8)) transistor_1 (.in({8{1'b1}}), .out(out_3), .gate(decoder_1_out0));
  Transistor #(.\type ("n"), .width(8)) transistor_2 (.in({8{1'b1}}), .out(out_6), .gate(decoder_1_out0));
  Transistor #(.\type ("n"), .width(8)) transistor_3 (.in({8{1'b1}}), .out(out_4), .gate(decoder_1_out0));
  Transistor #(.\type ("n"), .width(8)) transistor_4 (.in({8{1'b1}}), .out(out_7), .gate(decoder_1_out0));
  Transistor #(.\type ("n"), .width(8)) transistor_5 (.in({8{1'b1}}), .out(out_5), .gate(decoder_1_out0));
  Transistor #(.\type ("n"), .width(8)) transistor_6 (.in({8{1'b1}}), .out(out_9), .gate(decoder_1_out0));
  Transistor #(.\type ("n"), .width(8)) transistor_7 (.in({8{1'b1}}), .out(out_8), .gate(decoder_1_out0));
  Transistor #(.\type ("n"), .width(8)) transistor_8 (.in({8{1'b1}}), .out(out_10), .gate(decoder_1_out0));
  Transistor #(.\type ("n"), .width(8)) transistor_9 (.in({8{1'b1}}), .out(out_11), .gate(decoder_1_out0));
  Transistor #(.\type ("n"), .width(8)) transistor_10 (.in({8{1'b1}}), .out(out_12), .gate(decoder_1_out0));
  Transistor #(.\type ("n"), .width(8)) transistor_11 (.in({8{1'b1}}), .out(out_13), .gate(decoder_1_out0));
  Transistor #(.\type ("n"), .width(8)) transistor_12 (.in(8'he7), .out(out_3), .gate(decoder_1_out1));
  Transistor #(.\type ("n"), .width(8)) transistor_13 (.in(8'he7), .out(out_6), .gate(decoder_1_out1));
  Transistor #(.\type ("n"), .width(8)) transistor_14 (.in(8'he7), .out(out_5), .gate(decoder_1_out1));
  Transistor #(.\type ("n"), .width(8)) transistor_15 (.in(8'he7), .out(out_4), .gate(decoder_1_out1));
  Transistor #(.\type ("n"), .width(8)) transistor_16 (.in(8'he7), .out(out_10), .gate(decoder_1_out1));
  Transistor #(.\type ("n"), .width(8)) transistor_17 (.in({8{1'b0}}), .out(out_8), .gate(decoder_1_out1));
  Transistor #(.\type ("n"), .width(8)) transistor_18 (.in({8{1'b0}}), .out(out_9), .gate(decoder_1_out1));
  Transistor #(.\type ("n"), .width(8)) transistor_19 (.in({8{1'b0}}), .out(out_7), .gate(decoder_1_out1));
  Transistor #(.\type ("n"), .width(8)) transistor_20 (.in(8'he7), .out(out_12), .gate(decoder_1_out1));
  Transistor #(.\type ("n"), .width(8)) transistor_21 (.in(8'he7), .out(out_13), .gate(decoder_1_out1));
  Transistor #(.\type ("n"), .width(8)) transistor_22 (.in(8'he7), .out(out_11), .gate(decoder_1_out1));
  Transistor #(.\type ("n"), .width(8)) transistor_23 (.in(8'hf8), .out(out_5), .gate(decoder_1_out2));
  Transistor #(.\type ("n"), .width(8)) transistor_24 (.in({8{1'b0}}), .out(out_4), .gate(decoder_1_out2));
  Transistor #(.\type ("n"), .width(8)) transistor_25 (.in({8{1'b1}}), .out(out_3), .gate(decoder_1_out2));
  Transistor #(.\type ("n"), .width(8)) transistor_26 (.in(8'h6c), .out(out_6), .gate(decoder_1_out2));
  Transistor #(.\type ("n"), .width(8)) transistor_27 (.in(8'h6c), .out(out_10), .gate(decoder_1_out2));
  Transistor #(.\type ("n"), .width(8)) transistor_28 (.in(8'h56), .out(out_7), .gate(decoder_1_out2));
  Transistor #(.\type ("n"), .width(8)) transistor_29 (.in(8'hd3), .out(out_8), .gate(decoder_1_out2));
  Transistor #(.\type ("n"), .width(8)) transistor_30 (.in(8'h56), .out(out_9), .gate(decoder_1_out2));
  Transistor #(.\type ("n"), .width(8)) transistor_31 (.in({8{1'b1}}), .out(out_13), .gate(decoder_1_out2));
  Transistor #(.\type ("n"), .width(8)) transistor_32 (.in(8'hf8), .out(out_11), .gate(decoder_1_out2));
  Transistor #(.\type ("n"), .width(8)) transistor_33 (.in({8{1'b0}}), .out(out_12), .gate(decoder_1_out2));
  Transistor #(.\type ("n"), .width(8)) transistor_34 (.in(8'h91), .out(out_3), .gate(decoder_1_out3));
  Transistor #(.\type ("n"), .width(8)) transistor_35 (.in({8{1'b0}}), .out(out_4), .gate(decoder_1_out3));
  Transistor #(.\type ("n"), .width(8)) transistor_36 (.in(8'h6b), .out(out_8), .gate(decoder_1_out3));
  Transistor #(.\type ("n"), .width(8)) transistor_37 (.in(8'h18), .out(out_6), .gate(decoder_1_out3));
  Transistor #(.\type ("n"), .width(8)) transistor_38 (.in(8'h4a), .out(out_5), .gate(decoder_1_out3));
  Transistor #(.\type ("n"), .width(8)) transistor_39 (.in(8'h39), .out(out_7), .gate(decoder_1_out3));
  Transistor #(.\type ("n"), .width(8)) transistor_40 (.in(8'hc), .out(out_10), .gate(decoder_1_out3));
  Transistor #(.\type ("n"), .width(8)) transistor_41 (.in(8'hce), .out(out_9), .gate(decoder_1_out3));
  Transistor #(.\type ("n"), .width(8)) transistor_42 (.in(8'h80), .out(out_12), .gate(decoder_1_out3));
  Transistor #(.\type ("n"), .width(8)) transistor_43 (.in(8'h29), .out(out_11), .gate(decoder_1_out3));
  Transistor #(.\type ("n"), .width(8)) transistor_44 (.in(8'h12), .out(out_13), .gate(decoder_1_out3));
  Transistor #(.\type ("n"), .width(8)) transistor_45 (.in(8'hc0), .out(out_4), .gate(and_1_out));
  Transistor #(.\type ("n"), .width(8)) transistor_46 (.in(8'hc0), .out(out_3), .gate(and_1_out));
  Transistor #(.\type ("n"), .width(8)) transistor_47 (.in(8'hc0), .out(out_6), .gate(and_1_out));
  Transistor #(.\type ("n"), .width(8)) transistor_48 (.in(8'hc0), .out(out_5), .gate(and_1_out));
  Transistor #(.\type ("n"), .width(8)) transistor_49 (.in(8'hc0), .out(out_7), .gate(and_1_out));
  Transistor #(.\type ("n"), .width(8)) transistor_50 (.in(8'hc0), .out(out_8), .gate(and_1_out));
  Transistor #(.\type ("n"), .width(8)) transistor_51 (.in(8'hc0), .out(out_10), .gate(and_1_out));
  Transistor #(.\type ("n"), .width(8)) transistor_52 (.in(8'hc0), .out(out_9), .gate(and_1_out));
  Transistor #(.\type ("n"), .width(8)) transistor_53 (.in(8'hc0), .out(out_12), .gate(and_1_out));
  Transistor #(.\type ("n"), .width(8)) transistor_54 (.in(8'hc0), .out(out_11), .gate(and_1_out));
  Transistor #(.\type ("n"), .width(8)) transistor_55 (.in(8'hc0), .out(out_13), .gate(and_1_out));
  Transistor #(.\type ("n"), .width(8)) transistor_56 (.in(8'h3), .out(out_3), .gate(and_2_out));
  Transistor #(.\type ("n"), .width(8)) transistor_57 (.in(8'h3), .out(out_7), .gate(and_2_out));
  Transistor #(.\type ("n"), .width(8)) transistor_58 (.in(8'h3), .out(out_6), .gate(and_2_out));
  Transistor #(.\type ("n"), .width(8)) transistor_59 (.in(8'h3), .out(out_5), .gate(and_2_out));
  Transistor #(.\type ("n"), .width(8)) transistor_60 (.in(8'h3), .out(out_4), .gate(and_2_out));
  Transistor #(.\type ("n"), .width(8)) transistor_61 (.in(8'h3), .out(out_9), .gate(and_2_out));
  Transistor #(.\type ("n"), .width(8)) transistor_62 (.in(8'h3), .out(out_10), .gate(and_2_out));
  Transistor #(.\type ("n"), .width(8)) transistor_63 (.in(8'h3), .out(out_11), .gate(and_2_out));
  Transistor #(.\type ("n"), .width(8)) transistor_64 (.in(8'h3), .out(out_8), .gate(and_2_out));
  Transistor #(.\type ("n"), .width(8)) transistor_65 (.in(8'h3), .out(out_12), .gate(and_2_out));
  Transistor #(.\type ("n"), .width(8)) transistor_66 (.in(8'h3), .out(out_13), .gate(and_2_out));
  Transistor #(.width(8)) transistor_67 (.in({8{1'b0}}), .out(out_4), .gate(or_2_out));
  Transistor #(.width(8)) transistor_68 (.in({8{1'b0}}), .out(out_5), .gate(or_2_out));
  Transistor #(.width(8)) transistor_69 (.in({8{1'b0}}), .out(out_6), .gate(or_2_out));
  Transistor #(.width(8)) transistor_70 (.in({8{1'b0}}), .out(out_3), .gate(or_2_out));
  Transistor #(.width(8)) transistor_71 (.in({8{1'b0}}), .out(out_10), .gate(or_2_out));
  Transistor #(.width(8)) transistor_72 (.in({8{1'b0}}), .out(out_7), .gate(or_2_out));
  Transistor #(.width(8)) transistor_73 (.in({8{1'b0}}), .out(out_8), .gate(or_2_out));
  Transistor #(.width(8)) transistor_74 (.in({8{1'b0}}), .out(out_9), .gate(or_2_out));
  Transistor #(.width(8)) transistor_75 (.in({8{1'b0}}), .out(out_12), .gate(or_2_out));
  Transistor #(.width(8)) transistor_76 (.in({8{1'b0}}), .out(out_13), .gate(or_2_out));
  Transistor #(.width(8)) transistor_77 (.in({8{1'b0}}), .out(out_11), .gate(or_2_out));

  // Notes on the sheet:
  //   Транспорт
  //   2
  //   Щит
  //   3
  //   4
  //   Энергия
  //   Занята
  //   1
  //   Занята
  //   1
  //   Занята
  //   1
  //   Занята
  //   1
endmodule

module Player_Type (
  input  [1:0] in_1,
  input  [3:0] in_2,
  output [7:0] out_3,
  output [7:0] out_4,
  output [7:0] out_5,
  output [7:0] out_6,
  output [7:0] out_7,
  output [7:0] out_8,
  output [7:0] out_9,
  output [7:0] out_10,
  output [7:0] out_11,
  output [7:0] out_12,
  output [7:0] out_13,
  output [7:0] out_14,
  output [7:0] out_15,
  output [7:0] out_16,
  output [7:0] out_17,
  output [7:0] out_18,
  output [7:0] out_19,
  output [7:0] out_20,
  output [7:0] out_21,
  output [7:0] out_22,
  output [7:0] out_23,
  output [7:0] out_24
);

  wire and_5_out, and_6_out;
  wire [2:0] and_1_out;
  wire [3:0] and_3_out;

  and and_1 (and_1_out[0], in_1[0], in_2[0]);
  and and_2 (and_1_out[1], in_2[1], in_1[0]);
  and and_3 (and_3_out[0], in_1[1], in_2[0]);
  and and_4 (and_3_out[1], in_1[1], in_2[1]);
  xor xor_1 (and_3_out[3], in_2[3], and_6_out);
  xor xor_2 (and_1_out[2], in_2[2], and_5_out);
  and and_5 (and_5_out, in_1[0], in_2[2]);
  and and_6 (and_6_out, in_1[1], in_2[3]);
  DotMatrix #(.matrixcols(11), .matrixrows(8)) dotmatrix_1 (
    .col0(out_14), .col1(out_15), .col2(out_16), .col3(out_17), .col4(out_18), .col5(out_19), .col6(out_20),
    .col7(out_21), .col8(out_22), .col9(out_23), .col10(out_24));
  Type type_1 (
    .in_1(in_1[0]), .in_2({1'b0, and_1_out}), .out_3(out_14), .out_4(out_15), .out_5(out_16), .out_6(out_17),
    .out_7(out_18), .out_8(out_19), .out_9(out_20), .out_10(out_21), .out_11(out_22), .out_12(out_23),
    .out_13(out_24));
  DotMatrix #(.matrixcols(11), .matrixrows(8)) dotmatrix_2 (
    .col0(out_3), .col1(out_4), .col2(out_5), .col3(out_6), .col4(out_7), .col5(out_8), .col6(out_9),
    .col7(out_10), .col8(out_11), .col9(out_12), .col10(out_13));
  Type type_2 (
    .in_1(in_1[1]), .in_2({and_3_out[3], 1'b0, and_3_out[1:0]}), .out_3(out_3), .out_4(out_4), .out_5(out_5),
    .out_6(out_6), .out_7(out_7), .out_8(out_8), .out_9(out_9), .out_10(out_10), .out_11(out_11),
    .out_12(out_12), .out_13(out_13));

  // Notes on the sheet:
  //   Оранжевый
  //   Синий
endmodule

module Col_1 (
  input  D,
  input  C,
  input  B,
  input  A,
  output e,
  output d_2,
  output c_2,
  output b_2,
  output a_2
);

  wire and_1_out, and_2_out, and_3_out, and_4_out, and_5_out, and_6_out, and_7_out, and_8_out, and_9_out,
       and_10_out, and_11_out, and_12_out, and_13_out, and_14_out, and_15_out, and_16_out, and_17_out,
       and_18_out, not_1_out, not_2_out, not_3_out, not_4_out, not_5_out, not_6_out, not_7_out, not_8_out,
       not_9_out, not_10_out, not_11_out, not_12_out, not_13_out, not_14_out, not_15_out, not_16_out,
       not_17_out, not_18_out, not_19_out, not_20_out, not_21_out, not_22_out, not_23_out, not_24_out,
       not_25_out, not_26_out, not_27_out, not_28_out, not_29_out, not_30_out, not_31_out, not_32_out,
       not_33_out, not_34_out, not_35_out, not_36_out;

  not not_1 (not_1_out, D);
  and and_1 (and_1_out, not_1_out, not_2_out);
  not not_2 (not_2_out, C);
  not not_3 (not_3_out, C);
  and and_2 (and_2_out, not_3_out, not_4_out);
  not not_4 (not_4_out, B);
  not not_5 (not_5_out, D);
  not not_6 (not_6_out, B);
  and and_3 (and_3_out, not_5_out, not_6_out, A);
  not not_7 (not_7_out, D);
  and and_4 (and_4_out, not_7_out, B, not_8_out);
  not not_8 (not_8_out, A);
  not not_9 (not_9_out, D);
  not not_10 (not_10_out, C);
  and and_5 (and_5_out, not_9_out, not_10_out, not_11_out);
  not not_11 (not_11_out, A);
  not not_12 (not_12_out, C);
  and and_6 (and_6_out, not_12_out, not_13_out, not_14_out);
  not not_13 (not_13_out, B);
  not not_14 (not_14_out, A);
  not not_15 (not_15_out, D);
  and and_7 (and_7_out, not_15_out, B, not_16_out);
  not not_16 (not_16_out, A);
  not not_17 (not_17_out, D);
  and and_8 (and_8_out, not_17_out, not_18_out);
  not not_18 (not_18_out, A);
  not not_19 (not_19_out, D);
  and and_9 (and_9_out, not_19_out, not_20_out, B);
  not not_20 (not_20_out, C);
  not not_21 (not_21_out, D);
  and and_10 (and_10_out, not_21_out, C, not_22_out);
  not not_22 (not_22_out, B);
  not not_23 (not_23_out, C);
  and and_11 (and_11_out, D, not_23_out, not_24_out);
  not not_24 (not_24_out, B);
  not not_25 (not_25_out, D);
  and and_12 (and_12_out, not_25_out, not_26_out);
  not not_26 (not_26_out, B);
  not not_27 (not_27_out, C);
  and and_13 (and_13_out, not_27_out, not_28_out);
  not not_28 (not_28_out, B);
  not not_29 (not_29_out, D);
  and and_14 (and_14_out, not_29_out, C, not_30_out);
  not not_30 (not_30_out, A);
  not not_31 (not_31_out, D);
  and and_15 (and_15_out, not_31_out, not_32_out);
  not not_32 (not_32_out, A);
  not not_33 (not_33_out, D);
  and and_16 (and_16_out, not_33_out, B);
  not not_34 (not_34_out, D);
  and and_17 (and_17_out, not_34_out, C);
  not not_35 (not_35_out, C);
  and and_18 (and_18_out, D, not_35_out, not_36_out);
  not not_36 (not_36_out, B);
  or or_1 (e, and_1_out, and_2_out, and_3_out, and_4_out);
  or or_2 (d_2, and_5_out, and_6_out, and_7_out);
  or or_3 (c_2, and_8_out, and_9_out, and_10_out, and_11_out);
  or or_4 (b_2, and_12_out, and_13_out, and_14_out);
  or or_5 (a_2, and_15_out, and_16_out, and_17_out, and_18_out);
endmodule

module Col_2 (
  input  D,
  input  C,
  input  B,
  input  A,
  output e,
  output d_2,
  output c_2,
  output b_2,
  output a_2
);

  wire and_1_out, and_2_out, and_3_out, and_4_out, and_5_out, and_6_out, and_7_out, and_8_out, and_9_out,
       and_10_out, and_11_out, and_12_out, not_1_out, not_2_out, not_3_out, not_4_out, not_5_out, not_6_out,
       not_7_out, not_8_out, not_9_out, not_10_out, not_11_out, not_12_out, not_13_out, not_14_out,
       not_15_out, not_16_out, not_17_out, not_18_out, not_19_out, not_20_out, not_21_out, not_22_out,
       not_23_out, not_24_out, not_25_out, not_26_out, not_27_out, not_28_out;

  not not_1 (not_1_out, D);
  and and_1 (and_1_out, not_1_out, not_2_out);
  not not_2 (not_2_out, C);
  not not_3 (not_3_out, C);
  and and_2 (and_2_out, not_3_out, not_4_out);
  not not_4 (not_4_out, B);
  not not_5 (not_5_out, D);
  not not_6 (not_6_out, B);
  and and_3 (and_3_out, not_5_out, not_6_out, A);
  not not_7 (not_7_out, D);
  and and_4 (and_4_out, not_7_out, B, not_8_out);
  not not_8 (not_8_out, A);
  not not_9 (not_9_out, D);
  not not_10 (not_10_out, C);
  not not_11 (not_11_out, B);
  not not_12 (not_12_out, D);
  and and_5 (and_5_out, not_12_out, not_13_out, A);
  not not_13 (not_13_out, C);
  not not_14 (not_14_out, D);
  and and_6 (and_6_out, not_14_out, not_15_out, B);
  not not_15 (not_15_out, C);
  not not_16 (not_16_out, D);
  and and_7 (and_7_out, not_16_out, C, not_17_out);
  not not_17 (not_17_out, B);
  not not_18 (not_18_out, D);
  and and_8 (and_8_out, not_18_out, C, not_19_out);
  not not_19 (not_19_out, A);
  not not_20 (not_20_out, C);
  and and_9 (and_9_out, D, not_20_out, not_21_out);
  not not_21 (not_21_out, B);
  not not_22 (not_22_out, D);
  not not_23 (not_23_out, C);
  not not_24 (not_24_out, B);
  not not_25 (not_25_out, C);
  and and_10 (and_10_out, not_25_out, not_26_out);
  not not_26 (not_26_out, B);
  not not_27 (not_27_out, D);
  and and_11 (and_11_out, not_27_out, A);
  not not_28 (not_28_out, D);
  and and_12 (and_12_out, not_28_out, B);
  or or_1 (e, and_1_out, and_2_out, and_3_out, and_4_out);
  and and_13 (d_2, not_9_out, not_10_out, not_11_out, A);
  or or_2 (c_2, and_5_out, and_6_out, and_7_out, and_8_out, and_9_out);
  and and_14 (b_2, not_22_out, not_23_out, not_24_out, A);
  or or_3 (a_2, and_10_out, and_11_out, and_12_out);
endmodule

module Col_3 (
  input  D,
  input  C,
  input  B,
  input  A,
  output e,
  output d_2,
  output c_2,
  output b_2,
  output a_2
);

  wire and_1_out, and_2_out, and_3_out, and_4_out, and_5_out, and_6_out, and_7_out, and_8_out, and_9_out,
       and_10_out, and_11_out, and_12_out, and_13_out, and_14_out, and_15_out, and_16_out, and_17_out,
       not_1_out, not_2_out, not_3_out, not_4_out, not_5_out, not_6_out, not_7_out, not_8_out, not_9_out,
       not_10_out, not_11_out, not_12_out, not_13_out, not_14_out, not_15_out, not_16_out, not_17_out,
       not_18_out, not_19_out, not_20_out, not_21_out, not_22_out, not_23_out, not_24_out, not_25_out,
       not_26_out, not_27_out, not_28_out, not_29_out, not_30_out, not_31_out;

  not not_1 (not_1_out, D);
  not not_2 (not_2_out, C);
  and and_1 (and_1_out, not_2_out, not_3_out);
  not not_3 (not_3_out, B);
  not not_4 (not_4_out, D);
  and and_2 (and_2_out, not_4_out, not_5_out, not_6_out);
  not not_5 (not_5_out, B);
  not not_6 (not_6_out, A);
  not not_7 (not_7_out, D);
  and and_3 (and_3_out, not_7_out, B, A);
  not not_8 (not_8_out, D);
  and and_4 (and_4_out, not_8_out, C);
  not not_9 (not_9_out, C);
  and and_5 (and_5_out, D, not_9_out, not_10_out);
  not not_10 (not_10_out, B);
  not not_11 (not_11_out, D);
  and and_6 (and_6_out, not_11_out, not_12_out);
  not not_12 (not_12_out, A);
  not not_13 (not_13_out, D);
  and and_7 (and_7_out, not_13_out, B);
  not not_14 (not_14_out, D);
  and and_8 (and_8_out, not_14_out, C);
  not not_15 (not_15_out, C);
  and and_9 (and_9_out, D, not_15_out, not_16_out);
  not not_16 (not_16_out, B);
  not not_17 (not_17_out, D);
  and and_10 (and_10_out, not_17_out, not_18_out, not_19_out);
  not not_18 (not_18_out, C);
  not not_19 (not_19_out, A);
  not not_20 (not_20_out, D);
  not not_21 (not_21_out, B);
  and and_11 (and_11_out, not_20_out, not_21_out, not_22_out);
  not not_22 (not_22_out, A);
  not not_23 (not_23_out, D);
  and and_12 (and_12_out, not_23_out, B, A);
  and and_13 (and_13_out, D, not_24_out, not_25_out);
  not not_24 (not_24_out, C);
  not not_25 (not_25_out, B);
  not not_26 (not_26_out, D);
  and and_14 (and_14_out, not_26_out, not_27_out);
  not not_27 (not_27_out, A);
  not not_28 (not_28_out, D);
  and and_15 (and_15_out, not_28_out, B);
  not not_29 (not_29_out, D);
  and and_16 (and_16_out, not_29_out, C);
  not not_30 (not_30_out, C);
  and and_17 (and_17_out, D, not_30_out, not_31_out);
  not not_31 (not_31_out, B);
  or or_1 (e, not_1_out, and_1_out);
  or or_2 (d_2, and_2_out, and_3_out, and_4_out, and_5_out);
  or or_3 (c_2, and_6_out, and_7_out, and_8_out, and_9_out);
  or or_4 (b_2, and_10_out, and_11_out, and_12_out, and_13_out);
  or or_5 (a_2, and_14_out, and_15_out, and_16_out, and_17_out);
endmodule

module Numder (
  input  [9:0] in_1,
  output [4:0] out_2,
  output [4:0] out_3,
  output [4:0] out_4
);

  // Probe on {in_1[9:3], {3{in_1[3]}}}
  Col_1 col_1_1 (
    .D(in_1[3]), .C(in_1[3]), .B(in_1[3]), .A(in_1[3]), .e(out_2[4]), .d_2(out_2[3]), .c_2(out_2[2]),
    .b_2(out_2[1]), .a_2(out_2[0]));
  Col_2 col_2_1 (
    .D(in_1[3]), .C(in_1[3]), .B(in_1[3]), .A(in_1[3]), .e(out_3[4]), .d_2(out_3[3]), .c_2(out_3[2]),
    .b_2(out_3[1]), .a_2(out_3[0]));
  Col_3 col_3_1 (
    .D(in_1[3]), .C(in_1[3]), .B(in_1[3]), .A(in_1[3]), .e(out_4[4]), .d_2(out_4[3]), .c_2(out_4[2]),
    .b_2(out_4[1]), .a_2(out_4[0]));
  DotMatrix #(.matrixcols(3), .matrixrows(5)) dotmatrix_1 (.col0(out_2), .col1(out_3), .col2(out_4));

  assign in_1[2:0] = {3{in_1[3]}};
endmodule

module Output_Numder (
  input  [9:0] Energy,
  output [4:0] out_2,
  output [4:0] out_3,
  output [4:0] out_4,
  output [4:0] out_5,
  output [4:0] out_6,
  output [4:0] out_7,
  output [4:0] out_8,
  output [4:0] out_9,
  output [4:0] out_10,
  output [4:0] out_11,
  output [4:0] out_12
);

  // Probe on Energy
  BCD2 bcd2_1 (
    .in_1(Energy), .out_2(out_2), .out_3(out_3), .out_4(out_4), .out_5(out_6), .out_6(out_7), .out_7(out_8),
    .out_8(out_10), .out_9(out_11), .out_10(out_12));

  assign out_5 = {5{1'b0}};
  assign out_9 = {5{1'b0}};
endmodule

module Adding_Chip (
  input  A0,
  input  A1,
  input  A2,
  input  A3,
  output S0,
  output S1,
  output S2,
  output S3
);

  wire and_1_out, and_2_out, and_3_out, and_4_out, and_5_out, and_6_out, and_7_out, and_8_out, and_9_out,
       not_1_out, not_2_out, not_3_out, not_4_out;

  not not_1 (not_1_out, A3);
  not not_2 (not_2_out, A1);
  not not_3 (not_3_out, A2);
  not not_4 (not_4_out, A0);
  and and_1 (and_1_out, A2, A0);
  and and_2 (and_2_out, A2, A1);
  and and_3 (and_3_out, A2, not_2_out, not_4_out);
  and and_4 (and_4_out, A3, A0);
  and and_5 (and_5_out, not_3_out, A1);
  and and_6 (and_6_out, A1, A0);
  and and_7 (and_7_out, A3, not_4_out);
  and and_8 (and_8_out, A2, A1, not_4_out);
  and and_9 (and_9_out, not_1_out, not_3_out, A0);
  or or_1 (S3, and_1_out, and_2_out, A3);
  or or_2 (S2, and_3_out, and_4_out);
  or or_3 (S1, and_5_out, and_6_out, and_7_out);
  or or_4 (S0, and_7_out, and_8_out, and_9_out);
endmodule

module BCD2 (
  input  [9:0] in_1,
  output [4:0] out_2,
  output [4:0] out_3,
  output [4:0] out_4,
  output [4:0] out_5,
  output [4:0] out_6,
  output [4:0] out_7,
  output [4:0] out_8,
  output [4:0] out_9,
  output [4:0] out_10
);

  wire adding_chip_1_s0, adding_chip_1_s1, adding_chip_1_s2, adding_chip_2_s0, adding_chip_2_s1,
       adding_chip_2_s2, adding_chip_2_s3, adding_chip_3_s0, adding_chip_3_s1, adding_chip_3_s2,
       adding_chip_3_s3, adding_chip_4_s0, adding_chip_4_s1, adding_chip_4_s2, adding_chip_4_s3,
       adding_chip_5_s0, adding_chip_5_s1, adding_chip_5_s2, adding_chip_5_s3, adding_chip_6_s0,
       adding_chip_6_s1, adding_chip_6_s2, adding_chip_6_s3, adding_chip_7_s0, adding_chip_7_s1,
       adding_chip_7_s2, adding_chip_7_s3, adding_chip_8_s0, adding_chip_8_s1, adding_chip_8_s2,
       adding_chip_8_s3, adding_chip_9_s0, adding_chip_9_s1, adding_chip_9_s2, adding_chip_9_s3,
       adding_chip_10_s0, adding_chip_10_s1, adding_chip_10_s2, adding_chip_10_s3, adding_chip_11_s0,
       adding_chip_11_s1, adding_chip_11_s2, adding_chip_11_s3, adding_chip_12_s0, adding_chip_12_s1,
       adding_chip_12_s2, adding_chip_12_s3, and_1_out, or_1_out, or_2_out, or_3_out, or_4_out, or_5_out;
  wire [4:0] col_1_1_e, col_1_2_e, col_1_3_e, col_2_1_e, col_2_2_e, col_2_3_e, col_3_1_e, col_3_2_e,
       col_3_3_e;
  wire [9:0] transistor_4_out;

  Transistor #(.\type ("n"), .width(5)) transistor_1 (.in(col_1_1_e), .out(out_2), .gate(or_1_out));
  Col_1 col_1_1 (
    .D(adding_chip_1_s2), .C(adding_chip_1_s1), .B(adding_chip_1_s0), .A(adding_chip_11_s3),
    .e(col_1_1_e[0]), .d_2(col_1_1_e[1]), .c_2(col_1_1_e[2]), .b_2(col_1_1_e[3]), .a_2(col_1_1_e[4]));
  Transistor #(.\type ("n"), .width(5)) transistor_2 (.in(col_2_1_e), .out(out_3), .gate(or_1_out));
  DotMatrix #(.matrixcols(3), .matrixrows(5)) dotmatrix_1 (.col0(out_2), .col1(out_3), .col2(out_4));
  or or_1 (or_1_out, adding_chip_1_s2, adding_chip_1_s1, adding_chip_1_s0, adding_chip_11_s3);
  Col_2 col_2_1 (
    .D(adding_chip_1_s2), .C(adding_chip_1_s1), .B(adding_chip_1_s0), .A(adding_chip_11_s3),
    .e(col_2_1_e[0]), .d_2(col_2_1_e[1]), .c_2(col_2_1_e[2]), .b_2(col_2_1_e[3]), .a_2(col_2_1_e[4]));
  Transistor #(.\type ("n"), .width(5)) transistor_3 (.in(col_3_1_e), .out(out_4), .gate(or_1_out));
  Adding_Chip adding_chip_1 (
    .A0(adding_chip_10_s3), .A1(adding_chip_7_s3), .A2(adding_chip_5_s3), .A3(1'b0), .S0(adding_chip_1_s0),
    .S1(adding_chip_1_s1), .S2(adding_chip_1_s2));  // open: S3
  Col_3 col_3_1 (
    .D(adding_chip_1_s2), .C(adding_chip_1_s1), .B(adding_chip_1_s0), .A(adding_chip_11_s3),
    .e(col_3_1_e[0]), .d_2(col_3_1_e[1]), .c_2(col_3_1_e[2]), .b_2(col_3_1_e[3]), .a_2(col_3_1_e[4]));
  or or_2 (or_2_out, or_1_out, or_3_out);
  // Probe on in_1
  Transistor #(.width(10)) transistor_4 (.in(in_1), .out(transistor_4_out), .gate(and_1_out));
  Adding_Chip adding_chip_2 (
    .A0(transistor_4_out[7]), .A1(transistor_4_out[8]), .A2(transistor_4_out[9]), .A3(1'b0),
    .S0(adding_chip_2_s0), .S1(adding_chip_2_s1), .S2(adding_chip_2_s2), .S3(adding_chip_2_s3));
  Adding_Chip adding_chip_3 (
    .A0(transistor_4_out[6]), .A1(adding_chip_2_s0), .A2(adding_chip_2_s1), .A3(adding_chip_2_s2),
    .S0(adding_chip_3_s0), .S1(adding_chip_3_s1), .S2(adding_chip_3_s2), .S3(adding_chip_3_s3));
  Adding_Chip adding_chip_4 (
    .A0(transistor_4_out[5]), .A1(adding_chip_3_s0), .A2(adding_chip_3_s1), .A3(adding_chip_3_s2),
    .S0(adding_chip_4_s0), .S1(adding_chip_4_s1), .S2(adding_chip_4_s2), .S3(adding_chip_4_s3));
  Adding_Chip adding_chip_5 (
    .A0(adding_chip_4_s3), .A1(adding_chip_3_s3), .A2(adding_chip_2_s3), .A3(1'b0), .S0(adding_chip_5_s0),
    .S1(adding_chip_5_s1), .S2(adding_chip_5_s2), .S3(adding_chip_5_s3));
  Adding_Chip adding_chip_6 (
    .A0(transistor_4_out[4]), .A1(adding_chip_4_s0), .A2(adding_chip_4_s1), .A3(adding_chip_4_s2),
    .S0(adding_chip_6_s0), .S1(adding_chip_6_s1), .S2(adding_chip_6_s2), .S3(adding_chip_6_s3));
  Adding_Chip adding_chip_7 (
    .A0(adding_chip_6_s3), .A1(adding_chip_5_s0), .A2(adding_chip_5_s1), .A3(adding_chip_5_s2),
    .S0(adding_chip_7_s0), .S1(adding_chip_7_s1), .S2(adding_chip_7_s2), .S3(adding_chip_7_s3));
  Adding_Chip adding_chip_8 (
    .A0(transistor_4_out[3]), .A1(adding_chip_6_s0), .A2(adding_chip_6_s1), .A3(adding_chip_6_s2),
    .S0(adding_chip_8_s0), .S1(adding_chip_8_s1), .S2(adding_chip_8_s2), .S3(adding_chip_8_s3));
  Adding_Chip adding_chip_9 (
    .A0(transistor_4_out[2]), .A1(adding_chip_8_s0), .A2(adding_chip_8_s1), .A3(adding_chip_8_s2),
    .S0(adding_chip_9_s0), .S1(adding_chip_9_s1), .S2(adding_chip_9_s2), .S3(adding_chip_9_s3));
  Adding_Chip adding_chip_10 (
    .A0(adding_chip_8_s3), .A1(adding_chip_7_s0), .A2(adding_chip_7_s1), .A3(adding_chip_7_s2),
    .S0(adding_chip_10_s0), .S1(adding_chip_10_s1), .S2(adding_chip_10_s2), .S3(adding_chip_10_s3));
  Adding_Chip adding_chip_11 (
    .A0(adding_chip_9_s3), .A1(adding_chip_10_s0), .A2(adding_chip_10_s1), .A3(adding_chip_10_s2),
    .S0(adding_chip_11_s0), .S1(adding_chip_11_s1), .S2(adding_chip_11_s2), .S3(adding_chip_11_s3));
  Adding_Chip adding_chip_12 (
    .A0(transistor_4_out[1]), .A1(adding_chip_9_s0), .A2(adding_chip_9_s1), .A3(adding_chip_9_s2),
    .S0(adding_chip_12_s0), .S1(adding_chip_12_s1), .S2(adding_chip_12_s2), .S3(adding_chip_12_s3));
  or or_3 (or_3_out, adding_chip_11_s2, adding_chip_11_s1, adding_chip_11_s0, adding_chip_12_s3);
  Transistor #(.\type ("n"), .width(5)) transistor_5 (.in(col_1_2_e), .out(out_5), .gate(or_2_out));
  Transistor #(.\type ("n"), .width(5)) transistor_6 (.in(col_2_2_e), .out(out_6), .gate(or_2_out));
  DotMatrix #(.matrixcols(3), .matrixrows(5)) dotmatrix_2 (.col0(out_5), .col1(out_6), .col2(out_7));
  Transistor #(.\type ("n"), .width(10)) transistor_7 (.in(10'h3e7), .out(transistor_4_out), .gate(and_1_out));
  Col_1 col_1_2 (
    .D(adding_chip_11_s2), .C(adding_chip_11_s1), .B(adding_chip_11_s0), .A(adding_chip_12_s3),
    .e(col_1_2_e[0]), .d_2(col_1_2_e[1]), .c_2(col_1_2_e[2]), .b_2(col_1_2_e[3]), .a_2(col_1_2_e[4]));
  Transistor #(.\type ("n"), .width(5)) transistor_8 (.in(col_3_2_e), .out(out_7), .gate(or_2_out));
  and and_1 (and_1_out, in_1[9], in_1[8], in_1[7], in_1[6], in_1[5], or_5_out);
  or or_4 (or_4_out, adding_chip_1_s2, adding_chip_1_s1, adding_chip_1_s0, adding_chip_11_s3, adding_chip_11_s2, adding_chip_11_s1, adding_chip_11_s0, adding_chip_12_s3, adding_chip_12_s2, adding_chip_12_s1, adding_chip_12_s0, transistor_4_out[0]);
  Col_2 col_2_2 (
    .D(adding_chip_11_s2), .C(adding_chip_11_s1), .B(adding_chip_11_s0), .A(adding_chip_12_s3),
    .e(col_2_2_e[0]), .d_2(col_2_2_e[1]), .c_2(col_2_2_e[2]), .b_2(col_2_2_e[3]), .a_2(col_2_2_e[4]));
  Col_3 col_3_2 (
    .D(adding_chip_11_s2), .C(adding_chip_11_s1), .B(adding_chip_11_s0), .A(adding_chip_12_s3),
    .e(col_3_2_e[0]), .d_2(col_3_2_e[1]), .c_2(col_3_2_e[2]), .b_2(col_3_2_e[3]), .a_2(col_3_2_e[4]));
  or or_5 (or_5_out, in_1[4], in_1[3]);
  Transistor #(.\type ("n"), .width(5)) transistor_9 (.in(col_1_3_e), .out(out_8), .gate(or_4_out));
  DotMatrix #(.matrixcols(3), .matrixrows(5)) dotmatrix_3 (.col0(out_8), .col1(out_9), .col2(out_10));
  Col_2 col_2_3 (
    .D(adding_chip_12_s2), .C(adding_chip_12_s1), .B(adding_chip_12_s0), .A(transistor_4_out[0]),
    .e(col_2_3_e[0]), .d_2(col_2_3_e[1]), .c_2(col_2_3_e[2]), .b_2(col_2_3_e[3]), .a_2(col_2_3_e[4]));
  Col_1 col_1_3 (
    .D(adding_chip_12_s2), .C(adding_chip_12_s1), .B(adding_chip_12_s0), .A(transistor_4_out[0]),
    .e(col_1_3_e[0]), .d_2(col_1_3_e[1]), .c_2(col_1_3_e[2]), .b_2(col_1_3_e[3]), .a_2(col_1_3_e[4]));
  Transistor #(.\type ("n"), .width(5)) transistor_10 (.in(col_2_3_e), .out(out_9), .gate(or_4_out));
  Transistor #(.\type ("n"), .width(5)) transistor_11 (.in(col_3_3_e), .out(out_10), .gate(or_4_out));
  Col_3 col_3_3 (
    .D(adding_chip_12_s2), .C(adding_chip_12_s1), .B(adding_chip_12_s0), .A(transistor_4_out[0]),
    .e(col_3_3_e[0]), .d_2(col_3_3_e[1]), .c_2(col_3_3_e[2]), .b_2(col_3_3_e[3]), .a_2(col_3_3_e[4]));
  Transistor #(.width(5)) transistor_12 (.in({5{1'b0}}), .out(out_4), .gate(or_1_out));
  Transistor #(.width(5)) transistor_13 (.in({5{1'b0}}), .out(out_7), .gate(or_2_out));
  Transistor #(.width(5)) transistor_14 (.in({5{1'b0}}), .out(out_8), .gate(or_4_out));
  Transistor #(.width(5)) transistor_15 (.in({5{1'b0}}), .out(out_3), .gate(or_1_out));
  Transistor #(.width(5)) transistor_16 (.in({5{1'b0}}), .out(out_2), .gate(or_1_out));
  Transistor #(.width(5)) transistor_17 (.in({5{1'b0}}), .out(out_5), .gate(or_2_out));
  Transistor #(.width(5)) transistor_18 (.in({5{1'b0}}), .out(out_6), .gate(or_2_out));
  Transistor #(.width(5)) transistor_19 (.in({5{1'b0}}), .out(out_9), .gate(or_4_out));
  Transistor #(.width(5)) transistor_20 (.in({5{1'b0}}), .out(out_10), .gate(or_4_out));
endmodule

module inversion (
  input  [9:0] in_1,
  output [4:0] out_2,
  output [4:0] out_3,
  output [4:0] out_4,
  output [4:0] out_5,
  output [4:0] out_6,
  output [4:0] out_7,
  output [4:0] out_8,
  output [4:0] out_9,
  output [4:0] out_10,
  output [4:0] out_11,
  output [4:0] out_12
);

  wire nor_1_out;
  wire [4:0] output_numder_1_out_2, output_numder_1_out_3, output_numder_1_out_4, output_numder_1_out_5,
       output_numder_1_out_6, output_numder_1_out_7, output_numder_1_out_8, output_numder_1_out_9,
       output_numder_1_out_10, output_numder_1_out_11, output_numder_1_out_12, transistor_1_out,
       transistor_2_out, transistor_3_out, transistor_4_out, transistor_5_out, transistor_6_out,
       transistor_7_out, transistor_8_out, transistor_9_out, transistor_10_out, transistor_11_out;

  DotMatrix #(.matrixcols(11), .matrixrows(5)) dotmatrix_1 (
    .col0(out_2), .col1(out_3), .col2(out_4), .col3(out_5), .col4(out_6), .col5(out_7), .col6(out_8),
    .col7(out_9), .col8(out_10), .col9(out_11), .col10(out_12));
  nor nor_1 (nor_1_out, in_1[0], in_1[1], in_1[2], in_1[3], in_1[4], in_1[5], in_1[6], in_1[7], in_1[8], in_1[9]);
  Transistor #(.\type ("n"), .width(5)) transistor_1 (.in({5{1'b0}}), .out(transistor_1_out), .gate(nor_1_out));
  Transistor #(.\type ("n"), .width(5)) transistor_2 (.in(5'b01110), .out(transistor_2_out), .gate(nor_1_out));
  Transistor #(.\type ("n"), .width(5)) transistor_3 (.in(5'b01110), .out(transistor_3_out), .gate(nor_1_out));
  Transistor #(.\type ("n"), .width(5)) transistor_4 (.in(5'b01110), .out(transistor_4_out), .gate(nor_1_out));
  Transistor #(.\type ("n"), .width(5)) transistor_5 (.in(5'b01110), .out(transistor_5_out), .gate(nor_1_out));
  Transistor #(.\type ("n"), .width(5)) transistor_6 (.in(5'b01110), .out(transistor_6_out), .gate(nor_1_out));
  Transistor #(.\type ("n"), .width(5)) transistor_7 (.in(5'b01110), .out(transistor_7_out), .gate(nor_1_out));
  Transistor #(.\type ("n"), .width(5)) transistor_8 (.in(5'b01110), .out(transistor_8_out), .gate(nor_1_out));
  Transistor #(.\type ("n"), .width(5)) transistor_9 (.in(5'b01110), .out(transistor_9_out), .gate(nor_1_out));
  Transistor #(.\type ("n"), .width(5)) transistor_10 (.in(5'b01110), .out(transistor_10_out), .gate(nor_1_out));
  Transistor #(.\type ("n"), .width(5)) transistor_11 (.in({5{1'b0}}), .out(transistor_11_out), .gate(nor_1_out));
  Transistor #(.width(5)) transistor_12 (.in(output_numder_1_out_2), .out(transistor_1_out), .gate(nor_1_out));
  Output_Numder output_numder_1 (
    .Energy(in_1), .out_2(output_numder_1_out_2), .out_3(output_numder_1_out_3),
    .out_4(output_numder_1_out_4), .out_5(output_numder_1_out_5), .out_6(output_numder_1_out_6),
    .out_7(output_numder_1_out_7), .out_8(output_numder_1_out_8), .out_9(output_numder_1_out_9),
    .out_10(output_numder_1_out_10), .out_11(output_numder_1_out_11), .out_12(output_numder_1_out_12));
  Transistor #(.width(5)) transistor_13 (.in(output_numder_1_out_3), .out(transistor_4_out), .gate(nor_1_out));
  Transistor #(.width(5)) transistor_14 (.in(output_numder_1_out_6), .out(transistor_3_out), .gate(nor_1_out));
  Transistor #(.width(5)) transistor_15 (.in(output_numder_1_out_5), .out(transistor_5_out), .gate(nor_1_out));
  Transistor #(.width(5)) transistor_16 (.in(output_numder_1_out_4), .out(transistor_2_out), .gate(nor_1_out));
  assign out_8 = ~transistor_6_out;  // NOT_Gate not_1, 5 bits wide
  assign out_7 = ~transistor_7_out;  // NOT_Gate not_2, 5 bits wide
  assign out_6 = ~transistor_3_out;  // NOT_Gate not_3, 5 bits wide
  assign out_5 = ~transistor_5_out;  // NOT_Gate not_4, 5 bits wide
  assign out_4 = ~transistor_2_out;  // NOT_Gate not_5, 5 bits wide
  assign out_3 = ~transistor_4_out;  // NOT_Gate not_6, 5 bits wide
  assign out_2 = ~transistor_1_out;  // NOT_Gate not_7, 5 bits wide
  Transistor #(.width(5)) transistor_17 (.in(output_numder_1_out_8), .out(transistor_6_out), .gate(nor_1_out));
  Transistor #(.width(5)) transistor_18 (.in(output_numder_1_out_9), .out(transistor_8_out), .gate(nor_1_out));
  Transistor #(.width(5)) transistor_19 (.in(output_numder_1_out_7), .out(transistor_7_out), .gate(nor_1_out));
  Transistor #(.width(5)) transistor_20 (.in(output_numder_1_out_10), .out(transistor_9_out), .gate(nor_1_out));
  assign out_12 = ~transistor_11_out;  // NOT_Gate not_8, 5 bits wide
  assign out_11 = ~transistor_10_out;  // NOT_Gate not_9, 5 bits wide
  assign out_10 = ~transistor_9_out;  // NOT_Gate not_10, 5 bits wide
  assign out_9 = ~transistor_8_out;  // NOT_Gate not_11, 5 bits wide
  Transistor #(.width(5)) transistor_21 (.in(output_numder_1_out_12), .out(transistor_11_out), .gate(nor_1_out));
  Transistor #(.width(5)) transistor_22 (.in(output_numder_1_out_11), .out(transistor_10_out), .gate(nor_1_out));
endmodule

module full_diget_namber (
  input  [9:0] in_1,
  input  in_2,
  output [4:0] out_3,
  output [4:0] out_4,
  output [4:0] out_5,
  output [4:0] out_6,
  output [4:0] out_7,
  output [4:0] out_8,
  output [4:0] out_9,
  output [4:0] out_10,
  output [4:0] out_11,
  output [4:0] out_12,
  output [4:0] out_13
);

  wire [4:0] inversion_1_out_2, inversion_1_out_3, inversion_1_out_4, inversion_1_out_5, inversion_1_out_6,
       inversion_1_out_7, inversion_1_out_8, inversion_1_out_9, inversion_1_out_10, inversion_1_out_11,
       inversion_1_out_12, output_numder_1_out_2, output_numder_1_out_3, output_numder_1_out_4,
       output_numder_1_out_5, output_numder_1_out_6, output_numder_1_out_7, output_numder_1_out_8,
       output_numder_1_out_9, output_numder_1_out_10, output_numder_1_out_11, output_numder_1_out_12;

  DotMatrix #(.matrixcols(11), .matrixrows(5)) dotmatrix_1 (
    .col0(out_3), .col1(out_4), .col2(out_5), .col3(out_6), .col4(out_7), .col5(out_8), .col6(out_9),
    .col7(out_10), .col8(out_11), .col9(out_12), .col10(out_13));
  Transistor #(.\type ("n"), .width(5)) transistor_1 (.in(inversion_1_out_3), .out(out_4), .gate(in_2));
  Transistor #(.\type ("n"), .width(5)) transistor_2 (.in(inversion_1_out_2), .out(out_3), .gate(in_2));
  Transistor #(.\type ("n"), .width(5)) transistor_3 (.in(inversion_1_out_4), .out(out_5), .gate(in_2));
  Transistor #(.\type ("n"), .width(5)) transistor_4 (.in(inversion_1_out_5), .out(out_6), .gate(in_2));
  inversion inversion_1 (
    .in_1(in_1), .out_2(inversion_1_out_2), .out_3(inversion_1_out_3), .out_4(inversion_1_out_4),
    .out_5(inversion_1_out_5), .out_6(inversion_1_out_6), .out_7(inversion_1_out_7),
    .out_8(inversion_1_out_8), .out_9(inversion_1_out_9), .out_10(inversion_1_out_10),
    .out_11(inversion_1_out_11), .out_12(inversion_1_out_12));
  Transistor #(.\type ("n"), .width(5)) transistor_5 (.in(inversion_1_out_8), .out(out_9), .gate(in_2));
  Transistor #(.\type ("n"), .width(5)) transistor_6 (.in(inversion_1_out_10), .out(out_11), .gate(in_2));
  Transistor #(.\type ("n"), .width(5)) transistor_7 (.in(inversion_1_out_7), .out(out_8), .gate(in_2));
  Transistor #(.\type ("n"), .width(5)) transistor_8 (.in(inversion_1_out_9), .out(out_10), .gate(in_2));
  Transistor #(.\type ("n"), .width(5)) transistor_9 (.in(inversion_1_out_11), .out(out_12), .gate(in_2));
  Transistor #(.\type ("n"), .width(5)) transistor_10 (.in(inversion_1_out_12), .out(out_13), .gate(in_2));
  Transistor #(.\type ("n"), .width(5)) transistor_11 (.in(inversion_1_out_6), .out(out_7), .gate(in_2));
  Transistor #(.width(5)) transistor_12 (.in(output_numder_1_out_3), .out(out_4), .gate(in_2));
  Transistor #(.width(5)) transistor_13 (.in(output_numder_1_out_2), .out(out_3), .gate(in_2));
  Output_Numder output_numder_1 (
    .Energy(in_1), .out_2(output_numder_1_out_2), .out_3(output_numder_1_out_3),
    .out_4(output_numder_1_out_4), .out_5(output_numder_1_out_5), .out_6(output_numder_1_out_6),
    .out_7(output_numder_1_out_7), .out_8(output_numder_1_out_8), .out_9(output_numder_1_out_9),
    .out_10(output_numder_1_out_10), .out_11(output_numder_1_out_11), .out_12(output_numder_1_out_12));
  Transistor #(.width(5)) transistor_14 (.in(output_numder_1_out_10), .out(out_11), .gate(in_2));
  Transistor #(.width(5)) transistor_15 (.in(output_numder_1_out_4), .out(out_5), .gate(in_2));
  Transistor #(.width(5)) transistor_16 (.in(output_numder_1_out_11), .out(out_12), .gate(in_2));
  Transistor #(.width(5)) transistor_17 (.in(output_numder_1_out_7), .out(out_8), .gate(in_2));
  Transistor #(.width(5)) transistor_18 (.in(output_numder_1_out_8), .out(out_9), .gate(in_2));
  Transistor #(.width(5)) transistor_19 (.in(output_numder_1_out_9), .out(out_10), .gate(in_2));
  Transistor #(.width(5)) transistor_20 (.in(output_numder_1_out_6), .out(out_7), .gate(in_2));
  Transistor #(.width(5)) transistor_21 (.in(output_numder_1_out_5), .out(out_6), .gate(in_2));
  Transistor #(.width(5)) transistor_22 (.in(output_numder_1_out_12), .out(out_13), .gate(in_2));
endmodule

module Big_col_1 (
  input  Inversion,
  input  Zero,
  input  D,
  input  C,
  input  B,
  input  A,
  output [14:0] out_7
);

  wire and_1_out, and_2_out, and_3_out, and_4_out, and_5_out, and_6_out, and_7_out, and_8_out, and_9_out,
       and_10_out, and_11_out, and_12_out, and_13_out, and_14_out, and_15_out, and_16_out, and_17_out,
       and_18_out, and_19_out, not_1_out, not_2_out, not_3_out, not_4_out, not_5_out, not_6_out, not_7_out,
       not_8_out, not_9_out, not_10_out, not_11_out, not_12_out, not_13_out, not_14_out, not_15_out,
       not_16_out, not_17_out, not_18_out, not_19_out, not_20_out, not_21_out, not_22_out, not_23_out,
       not_24_out, not_25_out, not_26_out, not_27_out, not_28_out, not_29_out, not_30_out, not_31_out,
       not_32_out, not_33_out, not_34_out, not_35_out, not_36_out, or_1_out, or_2_out, or_3_out, or_4_out,
       or_5_out, or_6_out;
  wire [14:0] not_37_out;
  wire [14:2] and_20_out;

  not not_1 (not_1_out, D);
  and and_1 (and_1_out, not_1_out, not_2_out);
  not not_2 (not_2_out, C);
  not not_3 (not_3_out, C);
  and and_2 (and_2_out, not_3_out, not_4_out);
  not not_4 (not_4_out, B);
  not not_5 (not_5_out, D);
  and and_3 (and_3_out, not_5_out, not_6_out, A);
  not not_6 (not_6_out, B);
  not not_7 (not_7_out, D);
  and and_4 (and_4_out, not_7_out, B, not_8_out);
  not not_8 (not_8_out, A);
  not not_9 (not_9_out, D);
  not not_10 (not_10_out, C);
  and and_5 (and_5_out, not_9_out, not_10_out, not_11_out);
  not not_11 (not_11_out, A);
  not not_12 (not_12_out, C);
  not not_13 (not_13_out, B);
  and and_6 (and_6_out, not_12_out, not_13_out, not_14_out);
  not not_14 (not_14_out, A);
  not not_15 (not_15_out, D);
  and and_7 (and_7_out, not_15_out, B, not_16_out);
  not not_16 (not_16_out, A);
  not not_17 (not_17_out, D);
  not not_18 (not_18_out, A);
  not not_19 (not_19_out, D);
  not not_20 (not_20_out, C);
  not not_21 (not_21_out, D);
  not not_22 (not_22_out, B);
  not not_23 (not_23_out, C);
  not not_24 (not_24_out, B);
  not not_25 (not_25_out, D);
  not not_26 (not_26_out, B);
  not not_27 (not_27_out, C);
  not not_28 (not_28_out, B);
  not not_29 (not_29_out, D);
  not not_30 (not_30_out, A);
  not not_31 (not_31_out, D);
  not not_32 (not_32_out, A);
  not not_33 (not_33_out, D);
  not not_34 (not_34_out, D);
  not not_35 (not_35_out, C);
  not not_36 (not_36_out, B);
  and and_8 (and_8_out, A, C, ~B, D);  // AND_Gate
  or or_1 (or_1_out, and_1_out, and_2_out, and_3_out, and_4_out);
  or or_2 (or_2_out, and_5_out, and_6_out, and_7_out);
  and and_9 (and_9_out, not_17_out, not_18_out);
  and and_10 (and_10_out, not_19_out, not_20_out, B);
  and and_11 (and_11_out, not_21_out, C, not_22_out);
  and and_12 (and_12_out, D, not_23_out, not_24_out);
  and and_13 (and_13_out, not_25_out, not_26_out);
  and and_14 (and_14_out, not_27_out, not_28_out);
  or or_3 (or_3_out, and_13_out, and_14_out, and_15_out);
  and and_15 (and_15_out, not_29_out, C, not_30_out);
  and and_16 (and_16_out, not_31_out, not_32_out);
  and and_17 (and_17_out, not_33_out, B);
  and and_18 (and_18_out, not_34_out, C);
  and and_19 (and_19_out, D, not_35_out, not_36_out);
  or or_4 (or_4_out, and_9_out, and_10_out, and_11_out, and_12_out);
  or or_5 (or_5_out, and_16_out, and_17_out, and_18_out, and_19_out);
  and and_20 (and_20_out[2], Zero, or_1_out);
  and and_21 (and_20_out[5], Zero, or_2_out);
  and and_22 (and_20_out[11], Zero, or_3_out);
  and and_23 (and_20_out[14], Zero, or_5_out);
  and and_24 (and_20_out[8], Zero, or_6_out);
  or or_6 (or_6_out, or_4_out, and_8_out);
  Multiplexer #(.width(15), .enable("false")) multiplexer_1 (
    .in0({{3{and_20_out[14]}}, {3{and_20_out[11]}}, {3{and_20_out[8]}}, {3{and_20_out[5]}}, {3{and_20_out[2]}}}),
    .in1(not_37_out), .out(out_7), .sel(Inversion));
  assign not_37_out = ~{{3{and_20_out[14]}}, {3{and_20_out[11]}}, {3{and_20_out[8]}}, {3{and_20_out[5]}}, {3{and_20_out[2]}}};  // NOT_Gate not_37, 15 bits wide
endmodule

module Big_col_2 (
  input  Inversion,
  input  Zero,
  input  D,
  input  C,
  input  B,
  input  A,
  output [14:0] out_7
);

  wire and_1_out, and_2_out, and_3_out, and_4_out, and_5_out, and_6_out, and_7_out, and_8_out, and_9_out,
       and_10_out, and_11_out, and_12_out, and_13_out, and_14_out, and_15_out, not_1_out, not_2_out,
       not_3_out, not_4_out, not_5_out, not_6_out, not_7_out, not_8_out, not_9_out, not_10_out, not_11_out,
       not_12_out, not_13_out, not_14_out, not_15_out, not_16_out, not_17_out, not_18_out, not_19_out,
       not_20_out, not_21_out, not_22_out, not_23_out, not_24_out, not_25_out, not_26_out, not_27_out,
       not_28_out, or_1_out, or_2_out, or_3_out, or_4_out;
  wire [14:0] not_29_out;
  wire [14:2] and_16_out;

  not not_1 (not_1_out, D);
  not not_2 (not_2_out, C);
  not not_3 (not_3_out, C);
  not not_4 (not_4_out, B);
  not not_5 (not_5_out, D);
  not not_6 (not_6_out, B);
  not not_7 (not_7_out, D);
  not not_8 (not_8_out, A);
  not not_9 (not_9_out, D);
  not not_10 (not_10_out, C);
  not not_11 (not_11_out, B);
  not not_12 (not_12_out, D);
  not not_13 (not_13_out, C);
  not not_14 (not_14_out, D);
  not not_15 (not_15_out, C);
  not not_16 (not_16_out, D);
  not not_17 (not_17_out, B);
  not not_18 (not_18_out, D);
  not not_19 (not_19_out, A);
  not not_20 (not_20_out, C);
  not not_21 (not_21_out, B);
  not not_22 (not_22_out, D);
  not not_23 (not_23_out, C);
  not not_24 (not_24_out, B);
  not not_25 (not_25_out, C);
  not not_26 (not_26_out, B);
  not not_27 (not_27_out, D);
  not not_28 (not_28_out, D);
  and and_1 (and_1_out, not_1_out, not_2_out);
  and and_2 (and_2_out, not_3_out, not_4_out);
  and and_3 (and_3_out, not_5_out, not_6_out, A);
  and and_4 (and_4_out, not_7_out, B, not_8_out);
  and and_5 (and_5_out, not_9_out, not_10_out, not_11_out, A);
  and and_6 (and_6_out, not_12_out, not_13_out, A);
  and and_7 (and_7_out, not_14_out, not_15_out, B);
  and and_8 (and_8_out, not_16_out, C, not_17_out);
  and and_9 (and_9_out, not_18_out, C, not_19_out);
  and and_10 (and_10_out, D, not_20_out, not_21_out);
  and and_11 (and_11_out, not_22_out, not_23_out, not_24_out, A);
  and and_12 (and_12_out, not_25_out, not_26_out);
  and and_13 (and_13_out, not_27_out, A);
  and and_14 (and_14_out, not_28_out, B);
  or or_1 (or_1_out, and_1_out, and_2_out, and_3_out, and_4_out);
  or or_2 (or_2_out, and_6_out, and_7_out, and_8_out, and_9_out, and_10_out);
  or or_3 (or_3_out, and_12_out, and_13_out, and_14_out);
  and and_15 (and_15_out, A, C, ~B, D);  // AND_Gate
  and and_16 (and_16_out[2], Zero, or_1_out);
  and and_17 (and_16_out[5], and_5_out, Zero);
  and and_18 (and_16_out[8], Zero, or_4_out);
  or or_4 (or_4_out, or_2_out, and_15_out);
  and and_19 (and_16_out[11], and_11_out, Zero);
  and and_20 (and_16_out[14], or_3_out, Zero);
  assign not_29_out = ~{{3{and_16_out[14]}}, {3{and_16_out[11]}}, {3{and_16_out[8]}}, {3{and_16_out[5]}}, {3{and_16_out[2]}}};  // NOT_Gate not_29, 15 bits wide
  Multiplexer #(.width(15), .enable("false")) multiplexer_1 (
    .in0({{3{and_16_out[14]}}, {3{and_16_out[11]}}, {3{and_16_out[8]}}, {3{and_16_out[5]}}, {3{and_16_out[2]}}}),
    .in1(not_29_out), .out(out_7), .sel(Inversion));
endmodule

module Big_col_3 (
  input  Inversion,
  input  Zero,
  input  D,
  input  C,
  input  B,
  input  A,
  output [14:0] out_7
);

  wire and_1_out, and_2_out, and_3_out, and_4_out, and_5_out, and_6_out, and_7_out, and_8_out, and_9_out,
       and_10_out, and_11_out, and_12_out, and_13_out, and_14_out, and_15_out, and_16_out, and_17_out,
       and_18_out, not_1_out, not_2_out, not_3_out, not_4_out, not_5_out, not_6_out, not_7_out, not_8_out,
       not_9_out, not_10_out, not_11_out, not_12_out, not_13_out, not_14_out, not_15_out, not_16_out,
       not_17_out, not_18_out, not_19_out, not_20_out, not_21_out, not_22_out, not_23_out, not_24_out,
       not_25_out, not_26_out, not_27_out, not_28_out, not_29_out, not_30_out, not_31_out, or_1_out,
       or_2_out, or_3_out, or_4_out, or_5_out, or_6_out;
  wire [14:0] not_32_out;
  wire [14:2] and_19_out;

  not not_1 (not_1_out, C);
  not not_2 (not_2_out, B);
  not not_3 (not_3_out, D);
  not not_4 (not_4_out, B);
  not not_5 (not_5_out, A);
  not not_6 (not_6_out, D);
  not not_7 (not_7_out, D);
  not not_8 (not_8_out, C);
  not not_9 (not_9_out, B);
  not not_10 (not_10_out, D);
  not not_11 (not_11_out, A);
  not not_12 (not_12_out, D);
  not not_13 (not_13_out, D);
  not not_14 (not_14_out, C);
  not not_15 (not_15_out, B);
  not not_16 (not_16_out, D);
  not not_17 (not_17_out, C);
  not not_18 (not_18_out, A);
  not not_19 (not_19_out, D);
  not not_20 (not_20_out, B);
  not not_21 (not_21_out, A);
  not not_22 (not_22_out, D);
  not not_23 (not_23_out, C);
  not not_24 (not_24_out, B);
  not not_25 (not_25_out, D);
  not not_26 (not_26_out, A);
  not not_27 (not_27_out, D);
  not not_28 (not_28_out, D);
  not not_29 (not_29_out, C);
  not not_30 (not_30_out, B);
  not not_31 (not_31_out, D);
  and and_1 (and_1_out, not_1_out, not_2_out);
  and and_2 (and_2_out, not_3_out, not_4_out, not_5_out);
  and and_3 (and_3_out, not_6_out, B, A);
  and and_4 (and_4_out, not_7_out, C);
  and and_5 (and_5_out, D, not_8_out, not_9_out);
  and and_6 (and_6_out, not_10_out, not_11_out);
  and and_7 (and_7_out, not_12_out, B);
  and and_8 (and_8_out, not_13_out, C);
  and and_9 (and_9_out, D, not_14_out, not_15_out);
  and and_10 (and_10_out, not_16_out, not_17_out, not_18_out);
  and and_11 (and_11_out, not_19_out, not_20_out, not_21_out);
  and and_12 (and_12_out, not_22_out, B, A);
  and and_13 (and_13_out, D, not_23_out, not_24_out);
  and and_14 (and_14_out, not_25_out, not_26_out);
  and and_15 (and_15_out, not_27_out, B);
  and and_16 (and_16_out, not_28_out, C);
  and and_17 (and_17_out, D, not_29_out, not_30_out);
  and and_18 (and_18_out, A, C, ~B, D);  // AND_Gate
  or or_1 (or_1_out, not_31_out, and_1_out);
  or or_2 (or_2_out, and_2_out, and_3_out, and_4_out, and_5_out);
  or or_3 (or_3_out, and_6_out, and_7_out, and_8_out, and_9_out);
  or or_4 (or_4_out, and_10_out, and_11_out, and_12_out, and_13_out);
  or or_5 (or_5_out, and_14_out, and_15_out, and_16_out, and_17_out);
  and and_19 (and_19_out[2], Zero, or_1_out);
  and and_20 (and_19_out[5], Zero, or_2_out);
  or or_6 (or_6_out, or_3_out, and_18_out);
  and and_21 (and_19_out[8], Zero, or_6_out);
  and and_22 (and_19_out[11], Zero, or_4_out);
  and and_23 (and_19_out[14], or_5_out, Zero);
  Multiplexer #(.width(15), .enable("false")) multiplexer_1 (
    .in0({{3{and_19_out[14]}}, {3{and_19_out[11]}}, {3{and_19_out[8]}}, {3{and_19_out[5]}}, {3{and_19_out[2]}}}),
    .in1(not_32_out), .out(out_7), .sel(Inversion));
  assign not_32_out = ~{{3{and_19_out[14]}}, {3{and_19_out[11]}}, {3{and_19_out[8]}}, {3{and_19_out[5]}}, {3{and_19_out[2]}}};  // NOT_Gate not_32, 15 bits wide
endmodule

module Output_big_numder (
  input  INV,
  input  [6:0] in_2,
  output [14:0] out_3,
  output [14:0] out_4,
  output [14:0] out_5,
  output [14:0] out_6,
  output [14:0] out_7,
  output [14:0] out_8,
  output [14:0] out_9,
  output [14:0] out_10,
  output [14:0] out_11
);

  Big_col_1 big_col_1_1 (
    .Zero(in_2[5]), .D(in_2[3]), .C(in_2[2]), .B(in_2[1]), .A(in_2[0]), .out_7(out_3), .Inversion(INV));
  Big_col_2 big_col_2_1 (
    .Zero(in_2[5]), .D(in_2[3]), .C(in_2[2]), .B(in_2[1]), .A(in_2[0]), .out_7(out_6), .Inversion(INV));
  Big_col_3 big_col_3_1 (
    .Zero(in_2[5]), .D(in_2[3]), .C(in_2[2]), .B(in_2[1]), .A(in_2[0]), .out_7(out_9), .Inversion(INV));

  assign out_4 = out_3;
  assign out_5 = out_3;
  assign out_7 = out_6;
  assign out_8 = out_6;
  assign out_10 = out_9;
  assign out_11 = out_9;
endmodule

module Out_put_da_da_da (
  input  [6:0] in_1,
  input  [6:0] in_2,
  input  [6:0] in_3,
  input  [6:0] in_4
);

  wire [14:0] output_big_numder_1_p1, output_big_numder_1_p2, output_big_numder_1_p3, output_big_numder_1_p4,
       output_big_numder_1_p5, output_big_numder_1_p7, output_big_numder_1_p8, output_big_numder_1_p9,
       output_big_numder_1_p10, output_big_numder_1_p11, output_big_numder_1_p12, undriven, undriven_2,
       undriven_3, undriven_4, undriven_5, undriven_6, undriven_7, undriven_8, undriven_9, undriven_10,
       undriven_11, undriven_12, undriven_13, undriven_14, undriven_15, undriven_16, undriven_17,
       undriven_18, undriven_19, undriven_20, undriven_21, undriven_22, undriven_23, undriven_24, undriven_25;

  DotMatrix #(.matrixcols(9), .matrixrows(15)) dotmatrix_1 (
    .col0(output_big_numder_1_p1), .col1(output_big_numder_1_p2), .col2(output_big_numder_1_p3),
    .col3(output_big_numder_1_p4), .col4(output_big_numder_1_p5), .col5(output_big_numder_1_p7),
    .col6(output_big_numder_1_p8), .col7(output_big_numder_1_p9), .col8(output_big_numder_1_p10));
  // Output_big_numder output_big_numder_1: pin names not known; wires that end beside it: output_big_numder_1_p1, output_big_numder_1_p2, output_big_numder_1_p3, output_big_numder_1_p4, output_big_numder_1_p5, in_1, output_big_numder_1_p7, output_big_numder_1_p8, output_big_numder_1_p9, output_big_numder_1_p10, output_big_numder_1_p11, output_big_numder_1_p12
  DotMatrix #(.matrixcols(9), .matrixrows(15)) dotmatrix_2 (
    .col0(output_big_numder_1_p11), .col1(output_big_numder_1_p12), .col2(undriven), .col3(undriven_2),
    .col4(undriven_3), .col5(undriven_4), .col6(undriven_5), .col7(undriven_6), .col8(undriven_7));
  DotMatrix #(.matrixcols(9), .matrixrows(15)) dotmatrix_3 (
    .col0(undriven_8), .col1(undriven_9), .col2(undriven_10), .col3(undriven_11), .col4(undriven_12),
    .col5(undriven_13), .col6(undriven_14), .col7(undriven_15), .col8(undriven_16));
  DotMatrix #(.matrixcols(9), .matrixrows(15)) dotmatrix_4 (
    .col0(undriven_17), .col1(undriven_18), .col2(undriven_19), .col3(undriven_20), .col4(undriven_21),
    .col5(undriven_22), .col6(undriven_23), .col7(undriven_24), .col8(undriven_25));
endmodule
