// Logisim project people_controller.circ as structural Verilog: 2 circuits, main circuit main
module main (
  input  [4:0] in_1,
  input  in_2,
  input  in_3
);

  wire [1:0] controlled_buffer_1_out, controlled_buffer_2_out;
  wire [14:0] disign_1_out_3, disign_1_out_4, disign_1_out_5, disign_1_out_6, disign_1_out_7, disign_1_out_8,
       disign_1_out_9, disign_1_out_10, disign_1_out_11, disign_1_out_12, disign_1_out_13, disign_1_out_14,
       disign_1_out_15, disign_1_out_16, disign_1_out_17, disign_2_out_3, disign_2_out_4, disign_2_out_5,
       disign_2_out_6, disign_2_out_7, disign_2_out_8, disign_2_out_9, disign_2_out_10, disign_2_out_11,
       disign_2_out_12, disign_2_out_13, disign_2_out_14, disign_2_out_15, disign_2_out_16, disign_2_out_17;

  input_shifter input_shifter_1 (.MOSI(in_3), .CLK(in_2));  // open: Reset, Data_out, buffer_ptr
  assign controlled_buffer_1_out = in_1[4] ? in_1[1:0] : 2'bz;  // Controlled_Buffer controlled_buffer_1
  DotMatrix #(.matrixcols(15), .matrixrows(15)) dotmatrix_1 (
    .col0(disign_1_out_14), .col1(disign_1_out_9), .col2(disign_1_out_3), .col3(disign_1_out_15),
    .col4(disign_1_out_10), .col5(disign_1_out_4), .col6(disign_1_out_13), .col7(disign_1_out_8),
    .col8(disign_1_out_5), .col9(disign_1_out_16), .col10(disign_1_out_11), .col11(disign_1_out_6),
    .col12(disign_1_out_17), .col13(disign_1_out_12), .col14(disign_1_out_7));
  Disign disign_1 (
    .in_2(controlled_buffer_1_out), .out_14(disign_1_out_14), .out_9(disign_1_out_9), .out_3(disign_1_out_3),
    .out_15(disign_1_out_15), .out_10(disign_1_out_10), .out_4(disign_1_out_4), .out_13(disign_1_out_13),
    .out_8(disign_1_out_8), .out_5(disign_1_out_5), .out_16(disign_1_out_16), .out_11(disign_1_out_11),
    .out_6(disign_1_out_6), .out_17(disign_1_out_17), .out_12(disign_1_out_12), .out_7(disign_1_out_7),
    .in_1(in_1[2]));
  Disign disign_2 (
    .in_2(controlled_buffer_2_out), .out_14(disign_2_out_14), .out_9(disign_2_out_9), .out_3(disign_2_out_3),
    .out_15(disign_2_out_15), .out_10(disign_2_out_10), .out_4(disign_2_out_4), .out_13(disign_2_out_13),
    .out_8(disign_2_out_8), .out_5(disign_2_out_5), .out_16(disign_2_out_16), .out_11(disign_2_out_11),
    .out_6(disign_2_out_6), .out_17(disign_2_out_17), .out_12(disign_2_out_12), .out_7(disign_2_out_7),
    .in_1(in_1[3]));
  DotMatrix #(.matrixcols(15), .matrixrows(15)) dotmatrix_2 (
    .col0(disign_2_out_14), .col1(disign_2_out_9), .col2(disign_2_out_3), .col3(disign_2_out_15),
    .col4(disign_2_out_10), .col5(disign_2_out_4), .col6(disign_2_out_13), .col7(disign_2_out_8),
    .col8(disign_2_out_5), .col9(disign_2_out_16), .col10(disign_2_out_11), .col11(disign_2_out_6),
    .col12(disign_2_out_17), .col13(disign_2_out_12), .col14(disign_2_out_7));
  assign controlled_buffer_2_out = in_1[4] ? controlled_buffer_1_out : 2'bz;  // Controlled_Buffer controlled_buffer_2
endmodule

module Disign (
  input  in_1,
  input  [1:0] in_2,
  output [14:0] out_3,
  output [14:0] out_4,
  output [14:0] out_5,
  output [14:0] out_6,
  output [14:0] out_7,
  output [14:0] out_8,
  output [14:0] out_9,
  output [14:0] out_10,
  output [14:0] out_11,
  output [14:0] out_12,
  output [14:0] out_13,
  output [14:0] out_14,
  output [14:0] out_15,
  output [14:0] out_16,
  output [14:0] out_17
);

  wire decoder_1_out0, decoder_1_out1, decoder_1_out2, decoder_1_out3;
  wire [1:0] pull_resistor_1_node;

  Decoder #(.select(2), .enable("false")) decoder_1 (
    .out0(decoder_1_out0), .out1(decoder_1_out1), .out2(decoder_1_out2), .out3(decoder_1_out3),
    .sel(pull_resistor_1_node));
  Pull_Resistor pull_resistor_1 (.node(pull_resistor_1_node));
  assign pull_resistor_1_node = in_1 ? in_2 : 2'bz;  // Controlled_Buffer controlled_buffer_1
  DotMatrix #(.matrixcols(15), .matrixrows(15)) dotmatrix_1 (
    .col0(out_14), .col1(out_9), .col2(out_3), .col3(out_15), .col4(out_10), .col5(out_4), .col6(out_13),
    .col7(out_8), .col8(out_5), .col9(out_16), .col10(out_11), .col11(out_6), .col12(out_17), .col13(out_12),
    .col14(out_7));
  Transistor #(.\type ("n"), .width(15)) transistor_1 (.in({15{1'b0}}), .out(out_3), .gate(decoder_1_out0));
  Transistor #(.\type ("n"), .width(15)) transistor_2 (.in({15{1'b0}}), .out(out_9), .gate(decoder_1_out0));
  Transistor #(.\type ("n"), .width(15)) transistor_3 (.in({15{1'b0}}), .out(out_14), .gate(decoder_1_out0));
  Transistor #(.\type ("n"), .width(15)) transistor_4 (.in({15{1'b0}}), .out(out_15), .gate(decoder_1_out0));
  Transistor #(.\type ("n"), .width(15)) transistor_5 (.in({15{1'b0}}), .out(out_13), .gate(decoder_1_out0));
  Transistor #(.\type ("n"), .width(15)) transistor_6 (.in({15{1'b0}}), .out(out_10), .gate(decoder_1_out0));
  Transistor #(.\type ("n"), .width(15)) transistor_7 (.in({15{1'b0}}), .out(out_4), .gate(decoder_1_out0));
  Transistor #(.\type ("n"), .width(15)) transistor_8 (.in({15{1'b0}}), .out(out_8), .gate(decoder_1_out0));
  Transistor #(.\type ("n"), .width(15)) transistor_9 (.in({15{1'b0}}), .out(out_6), .gate(decoder_1_out0));
  Transistor #(.\type ("n"), .width(15)) transistor_10 (.in({15{1'b0}}), .out(out_11), .gate(decoder_1_out0));
  Transistor #(.\type ("n"), .width(15)) transistor_11 (.in({15{1'b0}}), .out(out_16), .gate(decoder_1_out0));
  Transistor #(.\type ("n"), .width(15)) transistor_12 (.in({15{1'b0}}), .out(out_5), .gate(decoder_1_out0));
  Transistor #(.\type ("n"), .width(15)) transistor_13 (.in({15{1'b0}}), .out(out_12), .gate(decoder_1_out0));
  Transistor #(.\type ("n"), .width(15)) transistor_14 (.in({15{1'b0}}), .out(out_17), .gate(decoder_1_out0));
  Transistor #(.\type ("n"), .width(15)) transistor_15 (.in({15{1'b0}}), .out(out_7), .gate(decoder_1_out0));
  Transistor #(.\type ("n"), .width(15)) transistor_16 (.in({15{1'b0}}), .out(out_14), .gate(decoder_1_out1));
  Transistor #(.\type ("n"), .width(15)) transistor_17 (.in(15'h2412), .out(out_3), .gate(decoder_1_out1));
  Transistor #(.\type ("n"), .width(15)) transistor_18 (.in(15'h180c), .out(out_9), .gate(decoder_1_out1));
  Transistor #(.\type ("n"), .width(15)) transistor_19 (.in(15'h23d6), .out(out_15), .gate(decoder_1_out1));
  Transistor #(.\type ("n"), .width(15)) transistor_20 (.in(15'h2aa2), .out(out_13), .gate(decoder_1_out1));
  Transistor #(.\type ("n"), .width(15)) transistor_21 (.in(15'h2aa2), .out(out_8), .gate(decoder_1_out1));
  Transistor #(.\type ("n"), .width(15)) transistor_22 (.in(15'h2a82), .out(out_4), .gate(decoder_1_out1));
  Transistor #(.\type ("n"), .width(15)) transistor_23 (.in(15'h383a), .out(out_10), .gate(decoder_1_out1));
  Transistor #(.\type ("n"), .width(15)) transistor_24 (.in(15'h2882), .out(out_11), .gate(decoder_1_out1));
  Transistor #(.\type ("n"), .width(15)) transistor_25 (.in(15'h2aa2), .out(out_16), .gate(decoder_1_out1));
  Transistor #(.\type ("n"), .width(15)) transistor_26 (.in(15'h2a22), .out(out_5), .gate(decoder_1_out1));
  Transistor #(.\type ("n"), .width(15)) transistor_27 (.in(15'h2c02), .out(out_6), .gate(decoder_1_out1));
  Transistor #(.\type ("n"), .width(15)) transistor_28 (.in({15{1'b0}}), .out(out_7), .gate(decoder_1_out1));
  Transistor #(.\type ("n"), .width(15)) transistor_29 (.in(15'h1838), .out(out_12), .gate(decoder_1_out1));
  Transistor #(.\type ("n"), .width(15)) transistor_30 (.in(15'h2bc4), .out(out_17), .gate(decoder_1_out1));
  Transistor #(.\type ("n"), .width(15)) transistor_31 (.in(15'h80), .out(out_14), .gate(decoder_1_out2));
  Transistor #(.\type ("n"), .width(15)) transistor_32 (.in(15'h220), .out(out_3), .gate(decoder_1_out2));
  Transistor #(.\type ("n"), .width(15)) transistor_33 (.in({15{1'b0}}), .out(out_15), .gate(decoder_1_out2));
  Transistor #(.\type ("n"), .width(15)) transistor_34 (.in(15'h140), .out(out_9), .gate(decoder_1_out2));
  Transistor #(.\type ("n"), .width(15)) transistor_35 (.in(15'h43e1), .out(out_8), .gate(decoder_1_out2));
  Transistor #(.\type ("n"), .width(15)) transistor_36 (.in(15'h21b2), .out(out_13), .gate(decoder_1_out2));
  Transistor #(.\type ("n"), .width(15)) transistor_37 (.in(15'h1084), .out(out_4), .gate(decoder_1_out2));
  Transistor #(.\type ("n"), .width(15)) transistor_38 (.in({15{1'b0}}), .out(out_10), .gate(decoder_1_out2));
  Transistor #(.\type ("n"), .width(15)) transistor_39 (.in(15'h1084), .out(out_16), .gate(decoder_1_out2));
  Transistor #(.\type ("n"), .width(15)) transistor_40 (.in(15'h26c2), .out(out_5), .gate(decoder_1_out2));
  Transistor #(.\type ("n"), .width(15)) transistor_41 (.in({15{1'b0}}), .out(out_11), .gate(decoder_1_out2));
  Transistor #(.\type ("n"), .width(15)) transistor_42 (.in({15{1'b0}}), .out(out_6), .gate(decoder_1_out2));
  Transistor #(.\type ("n"), .width(15)) transistor_43 (.in(15'h220), .out(out_17), .gate(decoder_1_out2));
  Transistor #(.\type ("n"), .width(15)) transistor_44 (.in(15'h80), .out(out_7), .gate(decoder_1_out2));
  Transistor #(.\type ("n"), .width(15)) transistor_45 (.in(15'h140), .out(out_12), .gate(decoder_1_out2));
  Transistor #(.\type ("n"), .width(15)) transistor_46 (.in(15'h100), .out(out_3), .gate(decoder_1_out3));
  Transistor #(.\type ("n"), .width(15)) transistor_47 (.in({15{1'b0}}), .out(out_14), .gate(decoder_1_out3));
  Transistor #(.\type ("n"), .width(15)) transistor_48 (.in({15{1'b0}}), .out(out_9), .gate(decoder_1_out3));
  Transistor #(.\type ("n"), .width(15)) transistor_49 (.in(15'h700), .out(out_10), .gate(decoder_1_out3));
  Transistor #(.\type ("n"), .width(15)) transistor_50 (.in(15'h1ffe), .out(out_13), .gate(decoder_1_out3));
  Transistor #(.\type ("n"), .width(15)) transistor_51 (.in(15'he00), .out(out_4), .gate(decoder_1_out3));
  Transistor #(.\type ("n"), .width(15)) transistor_52 (.in(15'h300), .out(out_15), .gate(decoder_1_out3));
  Transistor #(.\type ("n"), .width(15)) transistor_53 (.in(15'h700), .out(out_11), .gate(decoder_1_out3));
  Transistor #(.\type ("n"), .width(15)) transistor_54 (.in(15'he00), .out(out_16), .gate(decoder_1_out3));
  Transistor #(.\type ("n"), .width(15)) transistor_55 (.in(15'h3ffe), .out(out_8), .gate(decoder_1_out3));
  Transistor #(.\type ("n"), .width(15)) transistor_56 (.in(15'h1ffe), .out(out_5), .gate(decoder_1_out3));
  Transistor #(.\type ("n"), .width(15)) transistor_57 (.in(15'h100), .out(out_17), .gate(decoder_1_out3));
  Transistor #(.\type ("n"), .width(15)) transistor_58 (.in(15'h300), .out(out_6), .gate(decoder_1_out3));
  Transistor #(.\type ("n"), .width(15)) transistor_59 (.in({15{1'b0}}), .out(out_7), .gate(decoder_1_out3));
  Transistor #(.\type ("n"), .width(15)) transistor_60 (.in({15{1'b0}}), .out(out_12), .gate(decoder_1_out3));
endmodule
